// Logisim project arith_shift.circ as structural Verilog
module sshr_test (
  input  [7:0] a,
  input  [2:0] b,
  output [7:0] y
);

  Shifter #(.shift("ar")) shifter_1 (.in(a), .\dist (b), .out(y));
endmodule
