// Logisim project conv_ser_par.circ as structural Verilog
module conv_ser_par (
  input  clk,
  input  in,
  output [7:0] d,
  output rdy
);

  wire comparator_1_eq, eq_2_out, eq_6_out, in_2_p1, logical_and_1_p3, logical_not_1_p2, multiplexer_1_out,
       N19, N34, receive;
  wire [2:0] adder_1_out, logical_not_1_p1;
  wire [7:0] _1_b0_d_4_10_p1, d_p1, in_3_7_b0_p1, or_9_out;

  // BitLabeledTunnel #(.bitSpecs("N3")) in: pin names not known; wires that end beside it: in
  // BitLabeledTunnel #(.bitSpecs("N3"), .\output ("true")) in_2: pin names not known; wires that end beside it: in_2_p1
  Adder #(.width(3)) adder_1 (.a(logical_not_1_p1), .b(3'b001), .out(adder_1_out));  // open: cin, cout
  Register #(.width(1), .trigger("falling"), .resetType("syncReset"), .resetValue(1), .regHasEnable("false")) auto_33 (
    .D(N19), .Q(receive), .clk(clk), .clr(logical_and_1_p3));  // open: en
  not eq_6 (eq_6_out, in_2_p1);
  Comparator #(.width(3), .mode("unsigned")) comparator_1 (
    .a(logical_not_1_p1), .b(3'b111), .eq(comparator_1_eq));  // open: gt, lt
  // Logical_NOT_Gate #(.width(3)) logical_not_1: pin names not known; wires that end beside it: logical_not_1_p1, logical_not_1_p2
  Register #(.width(3), .trigger("falling"), .resetType("syncReset")) auto_37 (
    .D(adder_1_out), .en(receive), .Q(logical_not_1_p1), .clk(clk), .clr(logical_and_1_p3));
  not eq_2 (eq_2_out, receive);
  // Logical_AND_Gate #(.width(1)) logical_and_1: pin names not known; wires that end beside it: N34, eq_6_out, logical_and_1_p3
  // BitLabeledTunnel #(.width(8), .bitSpecs("N4,N5,N6,N7,N8,N9,N10,N11")) d: pin names not known; wires that end beside it: d_p1
  Register #(.trigger("falling"), .resetType("syncReset")) auto_35 (
    .D(or_9_out), .en(receive), .Q(d_p1), .clk(clk), .clr(logical_and_1_p3));
  // Logical_AND_Gate #(.width(1)) logical_and_2: pin names not known; wires that end beside it: logical_not_1_p2, eq_2_out, rdy
  // Logical_NOT_Gate #(.width(1)) logical_not_2: pin names not known; wires that end beside it: receive, N34
  // BitLabeledTunnel #(.width(8), .bitSpecs("0,N4,N5,N6,N7,N8,N9,N10"), .\output ("true")) _1_b0_d_4_10: pin names not known; wires that end beside it: _1_b0_d_4_10_p1
  assign or_9_out = _1_b0_d_4_10_p1 | in_3_7_b0_p1;  // OR_Gate or_9, 8 bits wide
  // BitLabeledTunnel #(.width(8), .bitSpecs("N3,0,0,0,0,0,0,0"), .\output ("true")) in_3_7_b0: pin names not known; wires that end beside it: in_3_7_b0_p1
  Multiplexer #(.enable("false")) multiplexer_1 (
    .in0(1'b1), .in1(1'b0), .out(multiplexer_1_out), .sel(comparator_1_eq));
  Multiplexer #(.enable("false")) multiplexer_2 (.in0(1'b0), .in1(multiplexer_1_out), .out(N19), .sel(receive));
  // BitLabeledTunnel #(.width(8), .bitSpecs("N4,N5,N6,N7,N8,N9,N10,N11"), .\output ("true")) d_2: pin names not known; wires that end beside it: d
endmodule
