// Logisim project conv_ser_par_handmade.circ as structural Verilog: 1 circuit, main circuit main
module main (
  input  in,
  output [7:0] d,
  output rdy
);

  wire and_res, clk, comparator_1_eq, comparator_2_eq, multiplexer_1_out, multiplexer_2_out, rec;
  wire [2:0] adder_1_out, counter_q;
  wire [7:0] bit_extender_1_out, or_1_out, shifter_1_out;

  Clock u_clk (.out(clk));
  and and_1 (and_res, ~in, ~rec);  // AND_Gate
  Register #(.width(3), .trigger("falling"), .resetType("syncReset")) counter (
    .D(adder_1_out), .en(rec), .Q(counter_q), .clk(clk), .clr(and_res));
  Adder #(.width(3)) adder_1 (.a(counter_q), .b(3'b001), .out(adder_1_out));  // open: cin, cout
  Comparator #(.width(3)) comparator_1 (.a(counter_q), .b(3'b111), .eq(comparator_1_eq));  // open: gt, lt
  Comparator #(.width(3)) comparator_2 (.a(counter_q), .b(3'b000), .eq(comparator_2_eq));  // open: gt, lt
  Register #(.trigger("falling"), .resetType("syncReset")) u_d (
    .D(or_1_out), .en(rec), .Q(d), .clk(clk), .clr(and_res));
  and and_2 (rdy, comparator_2_eq, ~rec);  // AND_Gate
  assign bit_extender_1_out = {{7{in}}, in};  // Bit_Extender bit_extender_1
  Shifter shifter_1 (.in(d), .\dist (3'b001), .out(shifter_1_out));
  // Probe on d
  Multiplexer #(.enable("false")) multiplexer_1 (
    .in0(1'b1), .in1(1'b0), .out(multiplexer_1_out), .sel(comparator_1_eq));
  assign or_1_out = bit_extender_1_out | shifter_1_out;  // OR_Gate or_1, 8 bits wide
  Multiplexer #(.enable("false")) multiplexer_2 (
    .in0(1'b0), .in1(multiplexer_1_out), .out(multiplexer_2_out), .sel(rec));
  Register #(.width(1), .trigger("falling"), .resetType("syncReset"), .resetValue(1), .regHasEnable("false")) receive (
    .D(multiplexer_2_out), .Q(rec), .clk(clk), .clr(and_res));  // open: en
endmodule
