// Logisim project counter.circ as structural Verilog
module counter (
  input  clk,
  input  reset,
  input  enable,
  output [3:0] count
);

  wire [3:0] adder_1_out;

  Adder #(.width(4)) adder_1 (.a(count), .b(4'b0001), .out(adder_1_out));  // open: cin, cout
  Register #(.width(4), .trigger("falling"), .resetType("syncReset")) auto_10 (
    .D(adder_1_out), .en(enable), .Q(count), .clk(clk), .clr(reset));
endmodule
