// Logisim project counter4b.circ as structural Verilog: 2 circuits, main circuit main
module main (
  output [3:0] out_1,
  output equals
);

  wire clock_1_out;
  wire [3:0] counter_1_q;

  Clock clock_1 (.out(clock_1_out));
  // Probe on out_1
  counter4b counter4b (.clk(clock_1_out), .value(out_1));
  Counter #(.width(4), .max('hf)) counter_1 (.Q(counter_1_q), .clk(clock_1_out));  // open: load, D, count, carry, clr
  // Probe on counter_1_q
  Comparator #(.width(4)) comparator_1 (.a(out_1), .b(counter_1_q), .eq(equals));  // open: gt, lt
endmodule

module counter4b (
  input  clk,
  output [3:0] value
);

  wire [3:0] adder_1_out;

  Adder #(.width(4)) adder_1 (.a(value), .b(4'b0001), .out(adder_1_out));  // open: cin, cout
  Register #(.width(4), .resetType("noReset"), .regHasEnable("false")) procdff_3 (
    .D(adder_1_out), .Q(value), .clk(clk));  // open: en, clr
endmodule
