// Logisim project examples_newcomponents.circ as structural Verilog: 1 circuit, main circuit main
module main (
  input  [7:0] A,
  input  [7:0] A_2,
  input  [7:0] B,
  input  [7:0] B_2,
  input  [7:0] A_3,
  input  [7:0] B_3,
  input  [7:0] A_4,
  input  [7:0] A_5,
  input  [7:0] B_4,
  input  [7:0] B_5,
  input  [7:0] A_6,
  input  [7:0] A_7,
  input  [7:0] B_6,
  input  [7:0] B_7,
  input  [7:0] A_8,
  input  [7:0] A_9,
  input  [7:0] A_10,
  input  [7:0] A_11,
  input  [7:0] B_8,
  input  [7:0] B_9,
  input  [7:0] A_12,
  input  [7:0] A_13,
  input  [2:0] B_10,
  input  [2:0] B_11,
  input  [7:0] A_14,
  input  [7:0] A_15,
  input  [2:0] B_12,
  input  [2:0] B_13,
  input  [7:0] A_16,
  input  [7:0] A_17,
  input  [15:0] A_18,
  input  [7:0] B_14,
  input  [7:0] S,
  input  [15:0] B_15,
  input  S_2,
  input  [1:0] S_3,
  input  [3:0] in_37,
  input  [3:0] in_38,
  output Y,
  output Y_2,
  output [7:0] Y_3,
  output Y_4,
  output Y_5,
  output Y_6,
  output Y_7,
  output Y_8,
  output Y_9,
  output Y_10,
  output Y_11,
  output [7:0] Y_12,
  output [7:0] Y_13,
  output [3:0] Y_14,
  output [3:0] Y_15,
  output [7:0] Y_16,
  output [7:0] Y_17,
  output [7:0] Y_18,
  output [7:0] out_57,
  output [3:0] out_58,
  output [3:0] out_59
);

  wire _2_p1, bitwise_multiplexer_1_p1, logical_and_1_p1;

  Register register_1 ();  // open: D, en, Q, clk, clr
  Adder adder_1 ();  // open: a, b, out, cin, cout
  Subtractor subtractor_1 ();  // open: a, b, out, bin, bout
  // Logical_OR_Gate logical_or_1: pin names not known; wires that end beside it: A, B, Y
  // Logical_OR_Gate logical_or_2: pin names not known; wires that end beside it: A_4, B_4, Y_4
  // Logical_AND_Gate logical_and_1: pin names not known; wires that end beside it: logical_and_1_p1, A_6, B_6, Y_6
  // Logical_AND_Gate logical_and_2: pin names not known; wires that end beside it: logical_and_1_p1, A_9, B_8, Y_10
  // Bitwise_Multiplexer bitwise_multiplexer_1: pin names not known; wires that end beside it: bitwise_multiplexer_1_p1, A_16, B_14, S, Y_16
  // BitLabeledTunnel #(.width(4), .bitSpecs("a,b,c,d")) _1: pin names not known; wires that end beside it: bitwise_multiplexer_1_p1, in_37
  // BitLabeledTunnel #(.width(4), .bitSpecs("e,f,g,h")) _2: pin names not known; wires that end beside it: _2_p1, in_38
  Negator negator_1 ();  // open: in, out
  Multiplier multiplier_1 ();  // open: a, b, out, cin, cout
  RAM ram_1 ();  // open: addr, data, sel, clk, ld, clr
  // Probe on A_12
  // Probe on B_10
  // Probe on A_14
  // Probe on B_12
  Divider divider_1 ();  // open: a, b, out, upper, rem
  // Probe on Y_12
  // Dynamic_Shifter dynamic_shifter_1: pin names not known; wires that end beside it: A_12, B_10, Y_12
  // Probe on Y_14
  // Dynamic_Shifter #(.yWidth(4), .mode("shiftx")) dynamic_shifter_2: pin names not known; wires that end beside it: A_14, B_12, Y_14
  // BitLabeledTunnel #(.width(8), .bitSpecs("a,b,c,d,e,f,g,h"), .\output ("true")) _3: pin names not known; wires that end beside it: out_57
  // BitLabeledTunnel #(.width(4), .bitSpecs("a,b,f,h"), .\output ("true")) _4: pin names not known; wires that end beside it: out_58
  // BitLabeledTunnel #(.width(4), .bitSpecs("a,h,b,g"), .\output ("true")) _5: pin names not known; wires that end beside it: out_59
  Comparator #(.strictEq("true")) comparator_1 ();  // open: a, b, gt, eq, lt
  // Logical_OR_Gate logical_or_3: pin names not known; wires that end beside it: A_2, B_2, Y_2, logical_and_1_p1
  // Logical_OR_Gate logical_or_4: pin names not known; wires that end beside it: A_5, B_5, Y_5
  // Logical_AND_Gate logical_and_3: pin names not known; wires that end beside it: A_7, B_7, Y_7
  // Logical_AND_Gate logical_and_4: pin names not known; wires that end beside it: A_10, B_9, Y_11
  // Priority_Multiplexer priority_multiplexer_1: pin names not known; wires that end beside it: A_17, B_15, S_3, Y_17
  // Probe on A_13
  // Probe on B_11
  // Probe on A_15
  // Probe on B_13
  // Probe on A_3
  // Exponent exponent_1: pin names not known; wires that end beside it: A_3, B_3, Y_3
  // Probe on B_3
  // Probe on Y_13
  // Dynamic_Shifter #(.bSigned("true")) dynamic_shifter_3: pin names not known; wires that end beside it: A_13, B_11, Y_13
  // Probe on Y_15
  // Dynamic_Shifter #(.yWidth(4), .mode("shiftx"), .bSigned("true")) dynamic_shifter_4: pin names not known; wires that end beside it: A_15, B_13, Y_15
  // Probe on Y_3
  // Logical_NOT_Gate logical_not_1: pin names not known; wires that end beside it: A_8, Y_8, logical_and_1_p1
  // Logical_NOT_Gate logical_not_2: pin names not known; wires that end beside it: A_11, Y_9, logical_and_1_p1
  // Binary_Multiplexer binary_multiplexer_1: pin names not known; wires that end beside it: A_18, S_2, Y_18, bitwise_multiplexer_1_p1, bitwise_multiplexer_1_p1, _2_p1

  // Notes on the sheet:
  //   Añadidos
  //   Modificados
  //   Sin signo
  //   Sin signo
  //   BABABABA
  //   >>
  //   >>
  //   Con signo
  //   Con signo
  //   <<
  //   <<
endmodule
