// Logisim project factorial.circ as structural Verilog: 4 circuits, main circuit main
module main (
  input  start,
  input  [7:0] n,
  output [31:0] f,
  output ready
);

  wire clk_out;

  Clock clk (.out(clk_out));
  // Probe on n
  factorial factorial (.clk(clk_out), .start(start), .n(n), .f(f), .ready(ready));
  // Probe on f
endmodule

module factorial (
  input  clk,
  input  start,
  input  [7:0] n,
  output [31:0] f,
  output ready
);

  wire mul_rdy, mul_start, store;
  wire [7:0] multiplexer_4_out, N53_60, RN_2_p1, RN_3_p1, RN_4_p1, RN_p1, subtractor_1_out;
  wire [31:0] N61_92, N125_156, RF, RN_45_52_24_b0_p1;

  // BitLabeledTunnel #(.width(8), .bitSpecs("N45,N46,N47,N48,N49,N50,N51,N52"), .\output ("true")) RN: pin names not known; wires that end beside it: RN_p1
  Register #(.width(32), .trigger("falling"), .resetType("noReset"), .regHasEnable("false")) procdff_11 (
    .D(N61_92), .Q(RF), .clk(clk));  // open: en, clr
  Comparator #(.mode("unsigned")) comparator_1 (.a(RN_p1), .b(8'h1), .lt(ready));  // open: gt, eq
  // BitLabeledTunnel #(.width(8), .bitSpecs("N45,N46,N47,N48,N49,N50,N51,N52"), .\output ("true")) RN_2: pin names not known; wires that end beside it: RN_2_p1
  Multiplexer #(.width(32), .enable("false")) multiplexer_1 (.in0(RF), .in1(N125_156), .out(N61_92), .sel(store));
  // BitLabeledTunnel #(.width(8), .bitSpecs("N45,N46,N47,N48,N49,N50,N51,N52")) RN_3: pin names not known; wires that end beside it: RN_3_p1
  Register #(.trigger("falling"), .resetType("noReset"), .regHasEnable("false")) procdff_10 (
    .D(N53_60), .Q(RN_3_p1), .clk(clk));  // open: en, clr
  Subtractor subtractor_1 (.a(RN_2_p1), .b(8'h1), .out(subtractor_1_out));  // open: bin, bout
  Multiplexer #(.width(32), .enable("false")) multiplexer_2 (.in0(f), .in1(32'h1), .out(N125_156), .sel(start));
  ctrl ctrl (.clk(clk), .start(start), .ready(ready), .mul_rdy(mul_rdy), .store(store), .mul_start(mul_start));
  // BitLabeledTunnel #(.width(8), .bitSpecs("N45,N46,N47,N48,N49,N50,N51,N52"), .\output ("true")) RN_4: pin names not known; wires that end beside it: RN_4_p1
  Multiplexer #(.width(8), .enable("false")) multiplexer_3 (
    .in0(RN_4_p1), .in1(multiplexer_4_out), .out(N53_60), .sel(store));
  // BitLabeledTunnel #(.width(32), .bitSpecs("N45,N46,N47,N48,N49,N50,N51,N52,0,0,0,0,0,0,0,0,0,0,0,0,0,0,0,0,0,0,0,0,0,0,0,0"), .\output ("true")) RN_45_52_24_b0: pin names not known; wires that end beside it: RN_45_52_24_b0_p1
  serial_multiplier mul (.clk(clk), .start(mul_start), .x(RN_45_52_24_b0_p1), .y(RF), .z(f), .ready(mul_rdy));
  Multiplexer #(.width(8), .enable("false")) multiplexer_4 (
    .in0(subtractor_1_out), .in1(n), .out(multiplexer_4_out), .sel(start));
endmodule

module ctrl (
  input  clk,
  input  start,
  input  ready,
  input  mul_rdy,
  output store,
  output mul_start
);

  wire comparator_2_eq, logical_and_1_p3, multiplexer_2_out, multiplexer_5_out, multiplexer_9_out,
       multiplexer_10_out, N11, N29;
  wire [2:0] multiplexer_1_out, multiplexer_3_out, N18_20, next, state;

  Comparator #(.width(3), .mode("unsigned")) comparator_1 (.a(state), .b(3'b010), .eq(N11));  // open: gt, lt
  Comparator #(.width(3), .mode("unsigned")) comparator_2 (
    .a(state), .b(3'b100), .eq(comparator_2_eq));  // open: gt, lt
  Multiplexer #(.width(3), .enable("false")) multiplexer_1 (
    .in0(N18_20), .in1(3'b100), .out(multiplexer_1_out), .sel(N11));
  Register #(.width(3), .trigger("falling"), .resetType("noReset"), .regHasEnable("false")) procdff_85 (
    .D(next), .Q(state), .clk(clk));  // open: en, clr
  Multiplexer #(.enable("false")) multiplexer_2 (.in0(1'b0), .in1(1'b1), .out(multiplexer_2_out), .sel(N11));
  // Logical_AND_Gate #(.width(1)) logical_and_1: pin names not known; wires that end beside it: comparator_2_eq, mul_rdy, logical_and_1_p3
  Multiplexer #(.width(3), .enable("false")) multiplexer_3 (
    .in0(multiplexer_1_out), .in1(3'b001), .out(multiplexer_3_out), .sel(ready));
  Multiplexer #(.enable("false")) multiplexer_4 (.in0(multiplexer_2_out), .in1(1'b0), .out(N29), .sel(ready));
  Multiplexer #(.enable("false")) multiplexer_5 (
    .in0(1'b0), .in1(1'b1), .out(multiplexer_5_out), .sel(logical_and_1_p3));
  Multiplexer #(.width(3), .enable("false")) multiplexer_6 (
    .in0(state), .in1(3'b010), .out(N18_20), .sel(logical_and_1_p3));
  Multiplexer #(.width(3), .enable("false")) multiplexer_7 (
    .in0(multiplexer_3_out), .in1(3'b010), .out(next), .sel(start));
  Multiplexer #(.enable("false")) multiplexer_8 (.in0(N29), .in1(1'b0), .out(mul_start), .sel(start));
  Multiplexer #(.enable("false")) multiplexer_9 (
    .in0(multiplexer_5_out), .in1(1'b0), .out(multiplexer_9_out), .sel(N11));
  Multiplexer #(.enable("false")) multiplexer_10 (
    .in0(multiplexer_9_out), .in1(1'b0), .out(multiplexer_10_out), .sel(ready));
  Multiplexer #(.enable("false")) multiplexer_11 (.in0(multiplexer_10_out), .in1(1'b1), .out(store), .sel(start));
endmodule

module serial_multiplier (
  input  clk,
  input  start,
  input  [31:0] x,
  input  [31:0] y,
  output [31:0] z,
  output ready
);

  wire RY_165_p1, RY_p1;
  wire [31:0] _1_b0_RX_229_259_p1, adder_1_out, multiplexer_1_out, multiplexer_2_out, multiplexer_3_out,
       N293_324, procdff_10_q, RX_2_p1, RY_2_p1, RY_166_196_1_b0_p1;

  // BitLabeledTunnel #(.width(32), .bitSpecs("N165,N166,N167,N168,N169,N170,N171,N172,N173,N174,N175,N176,N177,N178,N179,N180,N181,N182,N183,N184,N185,N186,N187,N188,N189,N190,N191,N192,N193,N194,N195,N196"), .\output ("true")) RY: pin names not known; wires that end beside it: RY_p1, RY_p1
  // Logical_NOT_Gate #(.width(32)) logical_not_1: pin names not known; wires that end beside it: ready
  // BitLabeledTunnel #(.width(32), .bitSpecs("N165,N166,N167,N168,N169,N170,N171,N172,N173,N174,N175,N176,N177,N178,N179,N180,N181,N182,N183,N184,N185,N186,N187,N188,N189,N190,N191,N192,N193,N194,N195,N196")) RY_2: pin names not known; wires that end beside it: RY_2_p1
  Register #(.width(32), .trigger("falling"), .resetType("noReset"), .regHasEnable("false")) procdff_11 (
    .D(multiplexer_1_out), .Q(RY_2_p1), .clk(clk));  // open: en, clr
  Register #(.width(32), .trigger("falling"), .resetType("noReset"), .regHasEnable("false")) procdff_10 (
    .D(multiplexer_2_out), .Q(procdff_10_q), .clk(clk));  // open: en, clr
  Adder #(.width(32)) adder_1 (.a(z), .b(multiplexer_3_out), .out(adder_1_out));  // open: cin, cout
  Register #(.width(32), .trigger("falling"), .resetType("noReset"), .regHasEnable("false")) procdff_12 (
    .D(N293_324), .Q(z), .clk(clk));  // open: en, clr
  // BitLabeledTunnel #(.width(32), .bitSpecs("N229,N230,N231,N232,N233,N234,N235,N236,N237,N238,N239,N240,N241,N242,N243,N244,N245,N246,N247,N248,N249,N250,N251,N252,N253,N254,N255,N256,N257,N258,N259,N260")) RX: pin names not known; wires that end beside it: procdff_10_q
  // BitLabeledTunnel #(.width(32), .bitSpecs("N166,N167,N168,N169,N170,N171,N172,N173,N174,N175,N176,N177,N178,N179,N180,N181,N182,N183,N184,N185,N186,N187,N188,N189,N190,N191,N192,N193,N194,N195,N196,0"), .\output ("true")) RY_166_196_1_b0: pin names not known; wires that end beside it: RY_166_196_1_b0_p1
  Multiplexer #(.width(32), .enable("false")) multiplexer_1 (
    .in0(RY_166_196_1_b0_p1), .in1(y), .out(multiplexer_1_out), .sel(start));
  // BitLabeledTunnel #(.width(32), .bitSpecs("0,N229,N230,N231,N232,N233,N234,N235,N236,N237,N238,N239,N240,N241,N242,N243,N244,N245,N246,N247,N248,N249,N250,N251,N252,N253,N254,N255,N256,N257,N258,N259"), .\output ("true")) _1_b0_RX_229_259: pin names not known; wires that end beside it: _1_b0_RX_229_259_p1
  Multiplexer #(.width(32), .enable("false")) multiplexer_2 (
    .in0(_1_b0_RX_229_259_p1), .in1(x), .out(multiplexer_2_out), .sel(start));
  Multiplexer #(.width(32), .enable("false")) multiplexer_3 (
    .in0({32{1'b0}}), .in1(RX_2_p1), .out(multiplexer_3_out), .sel(RY_165_p1));
  // BitLabeledTunnel #(.width(32), .bitSpecs("N229,N230,N231,N232,N233,N234,N235,N236,N237,N238,N239,N240,N241,N242,N243,N244,N245,N246,N247,N248,N249,N250,N251,N252,N253,N254,N255,N256,N257,N258,N259,N260"), .\output ("true")) RX_2: pin names not known; wires that end beside it: RX_2_p1
  // BitLabeledTunnel #(.bitSpecs("N165"), .\output ("true")) RY_165: pin names not known; wires that end beside it: RY_165_p1
  Multiplexer #(.width(32), .enable("false")) multiplexer_4 (
    .in0(adder_1_out), .in1({32{1'b0}}), .out(N293_324), .sel(start));

  // Other names for the same wires on the sheet: RZ[31:0] = z
endmodule
