// Logisim project factorial_handmade.circ as structural Verilog: 21 circuits, main circuit Uso factorial
module Uso_factorial (
  input  [7:0] in_1,
  input  start,
  input  start_2,
  input  [15:0] i,
  input  [15:0] i_2,
  output rdy,
  output res,
  output out_8,
  output out_9,
  output rdy_2,
  output p
);

  wire and_1_out, clk_2_out, clk_out, factorial_1_ready, factorial_v1_ready, factorial_v2_ready;
  wire [7:0] bit_extender_1_out, bit_extender_2_out;
  wire [31:0] and_2_out, factorial_1_f, factorial_v1_f, factorial_v2_f;

  Clock clk (.out(clk_out));
  // Probe on in_1
  // Probe on i
  Bit_Extender #(.in_width(16), .out_width(8)) bit_extender_1 (.in(i), .out(bit_extender_1_out));
  Bit_Extender #(.in_width(16), .out_width(8)) bit_extender_2 (.in(i_2), .out(bit_extender_2_out));
  Clock clk_2 (.out(clk_2_out));
  factorial_imported_v2 factorial_v1 (
    .clk(clk_2_out), .start(start), .n(in_1), .f(factorial_v1_f), .ready(factorial_v1_ready));
  factorial_imported_v2 factorial_v2 (
    .clk(clk_2_out), .start(start), .n(in_1), .f(factorial_v2_f), .ready(factorial_v2_ready));
  primegen primegen_1 (.i(i), .start(start_2), .n(i_2), .clk(clk_out), .p(out_8), .rdy(out_9));
  // Probe on i_2
  primegen_imported primegen_imported_1 (
    .clk(clk_out), .start(start_2), .k(bit_extender_1_out), .num(bit_extender_2_out), .rdy(rdy_2), .p(p));  // open: regI, regJ
  factorial factorial_1 (.n(in_1), .clk(clk_2_out), .start(start), .ready(factorial_1_ready), .f(factorial_1_f));
  // Probe on factorial_1_f
  // Probe on factorial_1_ready
  and and_1 (and_1_out, factorial_v2_ready, factorial_v1_ready);
  // Probe on factorial_v1_ready
  // Probe on factorial_v2_ready
  assign and_2_out = factorial_v1_f & factorial_v2_f;  // AND_Gate and_2, 32 bits wide
  // Probe on factorial_v1_f
  and and_3 (rdy, factorial_1_ready, and_1_out);
  Comparator #(.width(32)) comparator_1 (.a(factorial_1_f), .b(and_2_out), .eq(res));  // open: gt, lt

  // Notes on the sheet:
  //   Ejemplo de diseño modular: cálculo del factorial
  //   Ejemplo de diseño modular: cálculo de números primos
endmodule

module impl__multiplicador_serial (
  input  start,
  input  [31:0] y,
  input  [31:0] x,
  input  clk,
  output ready,
  output [31:0] z
);

  wire [31:0] adder_1_out, multiplexer_1_out, multiplexer_2_out, multiplexer_3_out, multiplexer_4_out, RX_q,
       RY_q, shifter_1_out, shifter_2_out;

  // Probe on x
  // Probe on y
  Shifter #(.width(32), .shift("lr")) shifter_1 (.in(RY_q), .\dist (5'b00001), .out(shifter_1_out));
  Shifter #(.width(32)) shifter_2 (.in(RX_q), .\dist (5'b00001), .out(shifter_2_out));
  Adder #(.width(32)) adder_1 (.a(multiplexer_4_out), .b(z), .out(adder_1_out));  // open: cin, cout
  Multiplexer #(.width(32), .enable("false")) multiplexer_1 (
    .in0(shifter_1_out), .in1(y), .out(multiplexer_1_out), .sel(start));
  Multiplexer #(.width(32), .enable("false")) multiplexer_2 (
    .in0(shifter_2_out), .in1(x), .out(multiplexer_2_out), .sel(start));
  Multiplexer #(.width(32), .enable("false")) multiplexer_3 (
    .in0(adder_1_out), .in1({32{1'b0}}), .out(multiplexer_3_out), .sel(start));
  Register #(.width(32), .trigger("falling")) RY (.D(multiplexer_1_out), .Q(RY_q), .clk(clk));  // open: en, clr
  Register #(.width(32), .trigger("falling")) RX (.D(multiplexer_2_out), .Q(RX_q), .clk(clk));  // open: en, clr
  Register #(.width(32), .trigger("falling")) RZ (.D(multiplexer_3_out), .Q(z), .clk(clk));  // open: en, clr
  Comparator #(.width(32)) comparator_1 (.a(RY_q), .b({32{1'b0}}), .eq(ready));  // open: gt, lt
  Multiplexer #(.width(32), .enable("false")) multiplexer_4 (
    .in0({32{1'b0}}), .in1(RX_q), .out(multiplexer_4_out), .sel(RY_q[0]));
  // Probe on z

  // Notes on the sheet:
  //   Multiplicador serial
  //   RY
  //   RX
  //   RZ
  //   RY>>1
  //   RX<<1
  //   RY[0] ? RX : 0
  //   ready=RY==0 ? 1 : 0
  //   int RZ= 0;
  //   int RX= x;
  //   int RY= y;
  //   while (RY!=0) {
  //   RX = RX<<1;
  //   RY= RY>>1;
  //   }
  //   return RZ;
  //   }
  //   RX=start ? x : RX<<1
  //   RY=start ? y : RY>>1
  //   int multiplicacion(int x, int y) { 
  //   RZ = RZ + (RY&1) ? RX : 0;
  //   RZ=start ? 0 : RZ+(RY[0] ? RX : 0)
endmodule

module factorial (
  input  [7:0] n,
  input  clk,
  input  start,
  output ready,
  output [31:0] f
);

  wire comparator_1_eq, comparator_1_lt, ctrl_mul_start, ctrl_store, mul_ready;
  wire [7:0] adder_1_out, multiplexer_1_out, RN_q;
  wire [31:0] bit_extender_1_out, mul_z, multiplexer_2_out;

  // Probe on n
  Adder adder_1 (.a(RN_q), .b({8{1'b1}}), .out(adder_1_out));  // open: cin, cout
  Multiplexer #(.width(8), .enable("false")) multiplexer_1 (
    .in0(adder_1_out), .in1(n), .out(multiplexer_1_out), .sel(start));
  Multiplexer #(.width(32), .enable("false")) multiplexer_2 (
    .in0(mul_z), .in1(32'h1), .out(multiplexer_2_out), .sel(start));
  Register #(.trigger("falling")) RN (.D(multiplexer_1_out), .en(ctrl_store), .Q(RN_q), .clk(clk));  // open: clr
  Register #(.width(32), .trigger("falling")) RF (
    .D(multiplexer_2_out), .en(ctrl_store), .Q(f), .clk(clk));  // open: clr
  Comparator comparator_1 (.a(RN_q), .b(8'h1), .eq(comparator_1_eq), .lt(comparator_1_lt));  // open: gt
  assign bit_extender_1_out = {{24{RN_q[7]}}, RN_q};  // Bit_Extender bit_extender_1
  Ctrl ctrl (
    .start(start), .ready(ready), .mul_rdy(mul_ready), .clk(clk), .store(ctrl_store),
    .mul_start(ctrl_mul_start));
  or or_1 (ready, comparator_1_eq, comparator_1_lt);
  impl__multiplicador_serial mul (
    .ready(mul_ready), .z(mul_z), .start(ctrl_mul_start), .y(bit_extender_1_out), .x(f), .clk(clk));
  // Probe on mul_z
  // Probe on f

  // Notes on the sheet:
  //   }
  //   }
  //   Cálculo de factorial con un multiplicador serial
  //   store
  //   int factorial(uchar n) {
  //   int f= 1;
  //   while (n>1) {
  //   f= f*n;
  //   n--;
  //   return f;
  //   estado Idle
  //   0**/0x -> Idle
  //   1**/1X -> Start
  //   estado Start
  //   1**/1x -> Start
  //   0**/01 -> Mul
  //   mul_start
  //   mul_rdy
  //   circuito secuencial de control
  //   start rdymul ready / store mul
  //   estado Mul
  //   000/00 -> Mul
  //   010/1x -> Start
  //   1**/1x -> Start
  //   0*1/0x -> Idle
  //   assign ready = RN <= 1
  //   always @(negedge clk)
  //   if (store) begin
  //   end
  //   RN <= start ? n : RN - 1
  //   RF <= start ? 1 : f
endmodule

module Ctrl (
  input  start,
  input  ready,
  input  mul_rdy,
  input  clk,
  output store,
  output mul_start
);

  wire ctrl_comb_1_d0, ctrl_comb_1_d1, d_ff_1_q, d_ff_2_q;

  D_Flip_Flop #(.trigger("falling")) d_ff_1 (.clk(clk), .D(ctrl_comb_1_d1), .Q(d_ff_1_q));  // open: Qn, preset, reset
  D_Flip_Flop #(.trigger("falling")) d_ff_2 (.clk(clk), .D(ctrl_comb_1_d0), .Q(d_ff_2_q));  // open: Qn, preset, reset
  Ctrl_comb ctrl_comb_1 (
    .q1(d_ff_1_q), .d1(ctrl_comb_1_d1), .q0(d_ff_2_q), .sta(start), .rmu(mul_rdy), .d0(ctrl_comb_1_d0),
    .rdy(ready), .sto(store), .mul(mul_start));

  // Notes on the sheet:
  //   Circuito de control secuencial
endmodule

module Ctrl_comb (
  input  q1,
  input  q0,
  input  sta,
  input  rmu,
  input  rdy,
  output d1,
  output d0,
  output sto,
  output mul
);

  wire and_1_out, and_2_out, and_3_out, and_4_out, not_1_out, not_2_out, not_3_out, not_4_out, not_5_out,
       not_6_out;

  not not_1 (not_1_out, sta);
  not not_2 (not_2_out, sta);
  not not_3 (not_3_out, rmu);
  not not_4 (not_4_out, rdy);
  not not_5 (not_5_out, rdy);
  not not_6 (not_6_out, rdy);
  not not_7 (mul, q1);
  and and_1 (and_1_out, q0, not_1_out);
  and and_2 (and_2_out, q1, not_2_out, not_3_out, not_4_out);
  and and_3 (and_3_out, q1, rmu, not_5_out);
  and and_4 (and_4_out, q1, rmu, not_6_out);
  or or_1 (d1, and_1_out, and_2_out);
  or or_2 (d0, sta, and_3_out);
  or or_3 (sto, sta, and_4_out);
endmodule

module memorias_ROM (
  input  [7:0] \dirección ,
  output [7:0] Valor_almacenado
);

  ROM rom_1 (.addr(\dirección ), .data(Valor_almacenado));
  // Probe on Valor_almacenado

  // Notes on the sheet:
  //   Son tablas de lectura en los circuitos
  //   Memorias ROM
  //   contents of rom_1 (hex, n*v repeats v):
  //   3 5 7 b d 11 13 17 1d 1f 25 29 2b 2f 35 3b 3d
endmodule

module Diccionario_en_ROM (
  input  start,
  input  [7:0] x,
  output not_found,
  output found
);

  wire and_1_out, clock_1_out, or_1_out;
  wire [7:0] adder_1_out, multiplexer_1_out, RegCnt_q, rom_1_data;

  Clock clock_1 (.out(clock_1_out));
  Adder adder_1 (.a(RegCnt_q), .b(8'h1), .out(adder_1_out));  // open: cin, cout
  or or_1 (or_1_out, start, and_1_out);
  Multiplexer #(.width(8), .disabled(0), .enable("false")) multiplexer_1 (
    .in0(adder_1_out), .in1({8{1'b0}}), .out(multiplexer_1_out), .sel(start));
  Register #(.trigger("falling")) RegCnt (
    .D(multiplexer_1_out), .en(or_1_out), .Q(RegCnt_q), .clk(clock_1_out));  // open: clr
  // Probe on RegCnt_q
  Comparator comparator_1 (.a(RegCnt_q), .b({8{1'b1}}), .eq(not_found));  // open: gt, lt
  and and_1 (and_1_out, ~not_found, ~found);  // AND_Gate
  ROM rom_1 (.addr(RegCnt_q), .data(rom_1_data));
  Comparator comparator_2 (.a(x), .b(rom_1_data), .eq(found));  // open: gt, lt

  // Notes on the sheet:
  //   Ejemplo: buscar un número en la ROM
  //   Diccionario en una ROM
  //   contents of rom_1 (hex, n*v repeats v):
  //   3 5 7 b d 11 13 17 1d 1f 25 29 2b 2f 35 3b 3d
  //   }
  //   }
  //   int buscar(int x) {
  //   int cnt= 0;
  //   while (cnt!=255) {
  //   return 0;
  //   if (rom[cnt]==x) return 1;
endmodule

module memorias_RAM (
  input  [7:0] \dirección ,
  input  [7:0] entrada,
  input  escribir,
  input  reloj,
  output [7:0] Valor_almacenado
);

  wire not_1_out;

  // Probe on entrada
  not not_1 (not_1_out, reloj);
  RAM #(.bus("separate")) ram_1 (
    .addr(\dirección ), .din(entrada), .data(Valor_almacenado), .str(escribir), .clk(not_1_out));  // open: sel, ld, clr
  // Probe on Valor_almacenado

  // Notes on the sheet:
  //   Memorias RAM
  //   Son los arreglos en los circuitos
endmodule

module Diccionario_en_RAM (
  input  start,
  input  [7:0] x,
  input  add,
  output not_found,
  output found
);

  wire and_1_out, clock_1_out, not_1_out, or_1_out;
  wire [7:0] adder_1_out, adder_2_out, multiplexer_1_out, multiplexer_2_out, ram_1_data, RegCnt_q, RegNext_q;

  Clock clock_1 (.out(clock_1_out));
  // Probe on x
  Adder adder_1 (.a(RegCnt_q), .b(8'h1), .out(adder_1_out));  // open: cin, cout
  Adder adder_2 (.a(8'h1), .b(RegNext_q), .out(adder_2_out));  // open: cin, cout
  or or_1 (or_1_out, start, and_1_out);
  Multiplexer #(.width(8), .disabled(0), .enable("false")) multiplexer_1 (
    .in0(adder_1_out), .in1({8{1'b0}}), .out(multiplexer_1_out), .sel(start));
  Register #(.trigger("falling")) RegCnt (
    .D(multiplexer_1_out), .en(or_1_out), .Q(RegCnt_q), .clk(clock_1_out));  // open: clr
  // Probe on RegCnt_q
  Register #(.trigger("falling")) RegNext (.D(adder_2_out), .en(add), .Q(RegNext_q), .clk(clock_1_out));  // open: clr
  Multiplexer #(.width(8), .disabled(0), .enable("false")) multiplexer_2 (
    .in0(RegCnt_q), .in1(RegNext_q), .out(multiplexer_2_out), .sel(add));
  Comparator #(.mode("unsigned")) comparator_1 (.a(RegCnt_q), .b(RegNext_q), .eq(not_found));  // open: gt, lt
  and and_1 (and_1_out, ~not_found, ~found);  // AND_Gate
  not not_1 (not_1_out, clock_1_out);
  RAM #(.bus("separate")) ram_1 (
    .addr(multiplexer_2_out), .din(x), .data(ram_1_data), .str(add), .clk(not_1_out));  // open: sel, ld, clr
  Comparator comparator_2 (.a(x), .b(ram_1_data), .eq(found));  // open: gt, lt

  // Notes on the sheet:
  //   buscar
  //   agregar
  //   Ejemplo: agregar o buscar
  //   un número en la RAM
  //   Diccionario en una RAM
  //   RAM
  //   int next= 0;
  //   int ram[256];
  //   }
  //   return 0;
  //   }
  //   }
  //   int buscar(int x) {
  //   int cnt= 0;
  //   while (cnt!=next) {
  //   int agregar(int x) {
  //   ram[next++]= x;
  //   if (ram[cnt]==x) return 1;
endmodule

module primegen_ctrl_comb (
  input  d1,
  input  d0,
  input  start,
  input  rdymark,
  input  rdy,
  input  not_prime,
  output q1,
  output q0,
  output startmark,
  output eni,
  output selmem
);

  wire and_1_out, and_2_out, and_3_out, and_4_out, and_5_out, and_7_out, and_8_out, and_9_out, not_1_out,
       not_2_out, not_3_out, not_4_out, not_5_out, not_6_out, not_7_out, not_8_out, not_9_out, not_10_out,
       not_11_out;

  not not_1 (not_1_out, rdy);
  not not_2 (not_2_out, not_prime);
  not not_3 (not_3_out, rdymark);
  not not_4 (not_4_out, d1);
  not not_5 (not_5_out, d0);
  not not_6 (not_6_out, rdy);
  not not_7 (not_7_out, rdy);
  not not_8 (not_8_out, d1);
  not not_9 (not_9_out, d0);
  not not_10 (not_10_out, rdy);
  not not_11 (not_11_out, rdymark);
  and and_1 (and_1_out, d0, not_1_out, not_2_out);
  and and_2 (and_2_out, d1, not_3_out);
  and and_3 (and_3_out, not_4_out, not_5_out, start);
  and and_4 (and_4_out, d0, not_6_out, not_prime);
  and and_5 (and_5_out, d1, rdymark);
  and and_6 (startmark, d0, not_7_out);
  and and_7 (and_7_out, not_8_out, not_9_out, start);
  and and_8 (and_8_out, d0, not_10_out, not_prime);
  and and_9 (and_9_out, d1, rdymark);
  and and_10 (selmem, d1, not_11_out);
  or or_1 (q1, and_1_out, and_2_out);
  or or_2 (q0, and_3_out, and_4_out, and_5_out);
  or or_3 (eni, and_7_out, and_8_out, and_9_out);
endmodule

module prime_gen_ctrl (
  input  clk,
  input  start,
  input  rdy_mark,
  input  rdy,
  input  nprime,
  output start_mark,
  output en_i,
  output str_mem
);

  wire d_ff_1_q, d_ff_2_q, primegen_ctrl_comb_1_q0, primegen_ctrl_comb_1_q1;

  D_Flip_Flop #(.trigger("falling")) d_ff_1 (
    .clk(clk), .D(primegen_ctrl_comb_1_q1), .Q(d_ff_1_q));  // open: Qn, preset, reset
  D_Flip_Flop #(.trigger("falling")) d_ff_2 (
    .clk(clk), .D(primegen_ctrl_comb_1_q0), .Q(d_ff_2_q));  // open: Qn, preset, reset
  primegen_ctrl_comb primegen_ctrl_comb_1 (
    .d1(d_ff_1_q), .d0(d_ff_2_q), .start(start), .rdymark(rdy_mark), .rdy(rdy), .not_prime(nprime),
    .q1(primegen_ctrl_comb_1_q1), .q0(primegen_ctrl_comb_1_q0), .startmark(start_mark), .eni(en_i),
    .selmem(str_mem));

  // Notes on the sheet:
  //   idle
  //   start-mark
  //   marking
  //   Ctrl states : start rdy-mark rdy ~prime / start-mark en-i str-mem -> state
  //   0 * * */ 0 0 0 -> idle
  //   1 * * * / 0 1 0 -> start-mark
  //   * * 0 0 / 1 0 0 -> marking
  //   * * 0 1 / 1 1 0 -> start-mark
  //   * * 1 * / 0 0 0 -> idle
  //   * 0 * * / 0 0 1 -> marking
  //   * 1 * * / 1 0 0 -> start-mark
endmodule

module primegen (
  input  [15:0] i,
  input  start,
  input  [15:0] n,
  input  clk,
  output p,
  output rdy
);

  wire and_1_out, and_2_out, d_ff_1_q, d_ff_2_q, mult_1_rdy, prime_gen_ctrl_1_en_i,
       prime_gen_ctrl_1_start_mark, prime_gen_ctrl_1_str_mem, ram_1_data;
  wire [15:0] adder_1_out, I_2_q, mult_1_j, multiplexer_1_out, multiplexer_2_out, multiplexer_3_out, N_q;

  Adder #(.width(16)) adder_1 (.a(I_2_q), .b(16'h2), .out(adder_1_out));  // open: cin, cout
  // Probe on i
  D_Flip_Flop #(.trigger("falling")) d_ff_1 (.clk(clk), .D(start), .Q(d_ff_1_q));  // open: Qn, preset, reset
  and and_1 (and_1_out, d_ff_1_q, ~d_ff_2_q);  // AND_Gate
  D_Flip_Flop #(.trigger("falling")) d_ff_2 (.clk(clk), .D(d_ff_1_q), .Q(d_ff_2_q));  // open: Qn, preset, reset
  // Probe on n
  Multiplexer #(.width(16), .disabled(0), .enable("false")) multiplexer_1 (
    .in0(adder_1_out), .in1(16'h3), .out(multiplexer_1_out), .sel(and_1_out));
  Register #(.width(16), .trigger("falling")) u_N (.D(n), .en(and_1_out), .Q(N_q), .clk(clk));  // open: clr
  // Probe on I_2_q
  Register #(.width(16), .trigger("falling")) I_2 (
    .D(multiplexer_1_out), .en(prime_gen_ctrl_1_en_i), .Q(I_2_q), .clk(clk));  // open: clr
  // Probe on mult_1_j
  mult mult_1 (.i(I_2_q), .start(prime_gen_ctrl_1_start_mark), .clk(clk), .n(N_q), .j(mult_1_j), .rdy(mult_1_rdy));
  Comparator #(.width(16), .mode("unsigned")) comparator_1 (.a(I_2_q), .b(N_q), .gt(rdy));  // open: eq, lt
  Multiplexer #(.width(16), .disabled(0), .enable("false")) multiplexer_2 (
    .in0(mult_1_j), .in1(I_2_q), .out(multiplexer_2_out), .sel(prime_gen_ctrl_1_start_mark));
  // Probe on multiplexer_3_out
  Multiplexer #(.width(16), .disabled(0), .enable("false")) multiplexer_3 (
    .in0(multiplexer_2_out), .in1(i), .out(multiplexer_3_out), .sel(rdy));
  prime_gen_ctrl prime_gen_ctrl_1 (
    .clk(clk), .start(and_1_out), .rdy_mark(mult_1_rdy), .rdy(rdy), .nprime(ram_1_data),
    .start_mark(prime_gen_ctrl_1_start_mark), .en_i(prime_gen_ctrl_1_en_i), .str_mem(prime_gen_ctrl_1_str_mem));
  RAM #(.addrWidth(16), .dataWidth(1), .bus("separate")) ram_1 (
    .addr(multiplexer_3_out), .din(1'b1), .data(ram_1_data), .str(prime_gen_ctrl_1_str_mem), .sel(1'b1),
    .clk(clk), .ld(1'b1), .clr(and_2_out));
  and and_2 (and_2_out, clk, and_1_out);
  not not_1 (p, ram_1_data);

  // Notes on the sheet:
  //   Cálculo de los números primos
  //   idle
  //   start-mark
  //   marking
  //   Ctrl states : start rdy-mark rdy ~prime / start-mark en-i str-mem -> state
  //   0 * * */ 0 0 0 -> idle
  //   1 * * * / 0 1 0 -> start-mark
  //   * * 0 0 / 1 0 0 -> marking
  //   * * 0 1 / 1 1 0 -> start-mark
  //   * * 1 * / 0 0 0 -> idle
  //   * 0 * * / 0 0 1 -> marking
  //   * 1 * * / 1 0 0 -> start-mark
  //   1 if i is a prime number
  //   0 if i is a prime number
endmodule

module mult (
  input  [15:0] i,
  input  start,
  input  clk,
  input  [15:0] n,
  output [15:0] j,
  output rdy
);

  wire or_1_out;
  wire [15:0] adder_1_out, multiplexer_1_out;

  // Probe on i
  Multiplexer #(.width(16), .disabled(0), .enable("false")) multiplexer_1 (
    .in0(j), .in1(i), .out(multiplexer_1_out), .sel(start));
  // Probe on n
  Adder #(.width(16)) adder_1 (.a(multiplexer_1_out), .b(i), .out(adder_1_out));  // open: cin, cout
  or or_1 (or_1_out, start, ~rdy);  // OR_Gate
  // Probe on j
  Register #(.width(16), .trigger("falling")) u_J (.D(adder_1_out), .en(or_1_out), .Q(j), .clk(clk));  // open: clr
  Comparator #(.width(16), .mode("unsigned")) comparator_1 (.a(j), .b(n), .gt(rdy));  // open: eq, lt
endmodule

module factorial_imported_v2 (
  input  clk,
  input  start,
  input  [7:0] n,
  output [31:0] f,
  output ready
);

  wire ctrl_mul_start, mul_ready, store;
  wire [7:0] auto_12_q, multiplexer_1_out, RN_2_p1, RN_3_p1, subtractor_1_out;
  wire [31:0] RF, RN_54_61_24_b0_p1;

  Register #(.trigger("falling"), .resetType("noReset")) auto_12 (
    .D(multiplexer_1_out), .en(store), .Q(auto_12_q), .clk(clk));  // open: clr
  // BitLabeledTunnel #(.width(8), .bitSpecs("N54,N55,N56,N57,N58,N59,N60,N61")) RN: pin names not known; wires that end beside it: auto_12_q
  // BitLabeledTunnel #(.width(8), .bitSpecs("N54,N55,N56,N57,N58,N59,N60,N61"), .\output ("true")) RN_2: pin names not known; wires that end beside it: RN_2_p1
  Comparator #(.mode("unsigned")) comparator_1 (.a(RN_2_p1), .b(8'h1), .lt(ready));  // open: gt, eq
  // BitLabeledTunnel #(.width(8), .bitSpecs("N54,N55,N56,N57,N58,N59,N60,N61"), .\output ("true")) RN_3: pin names not known; wires that end beside it: RN_3_p1
  Register #(.width(32), .trigger("falling"), .resetType("syncReset"), .resetValue(1)) auto_14 (
    .D(f), .en(store), .Q(RF), .clk(clk), .clr(start));
  ctrl ctrl (.clk(clk), .start(start), .ready(ready), .mul_rdy(mul_ready), .store(store), .mul_start(ctrl_mul_start));
  Subtractor subtractor_1 (.a(RN_3_p1), .b(8'h1), .out(subtractor_1_out));  // open: bin, bout
  // BitLabeledTunnel #(.width(32), .bitSpecs("N54,N55,N56,N57,N58,N59,N60,N61,0,0,0,0,0,0,0,0,0,0,0,0,0,0,0,0,0,0,0,0,0,0,0,0"), .\output ("true")) RN_54_61_24_b0: pin names not known; wires that end beside it: RN_54_61_24_b0_p1
  serial_multiplier mul (.clk(clk), .start(ctrl_mul_start), .x(RN_54_61_24_b0_p1), .y(RF), .z(f), .ready(mul_ready));
  Multiplexer #(.width(8), .enable("false")) multiplexer_1 (
    .in0(subtractor_1_out), .in1(n), .out(multiplexer_1_out), .sel(start));
endmodule

module ctrl (
  input  clk,
  input  start,
  input  ready,
  input  mul_rdy,
  output store,
  output mul_start
);

  wire auto_89_y, auto_93_y, auto_96_y, comparator_1_eq, multiplexer_2_out, multiplexer_3_out,
       multiplexer_6_out, multiplexer_7_out, multiplexer_8_out, N13_p1, N17_2_p1, N17_3_p1, N17_4_p1, N17_p1,
       N18_2_p1, N18_3_p1, N18_p1, ready_2_p1, ready_3_p1, ready_4_p1, start_2_p1, start_3_p1, start_4_p1,
       state_15_p1;
  wire [1:0] auto_91_q, N3_4_p1, N8_9_p1, N17_18_p1;
  wire [2:0] multiplexer_4_out, multiplexer_5_out, N4_17_18_p1, N13_24_25_2_p1, N13_24_25_p1, state_2_p1,
       state_p1, X_UNDEF_3_9918_p1;

  // BitLabeledTunnel #(.bitSpecs("N3")) start: pin names not known; wires that end beside it: start
  // BitLabeledTunnel #(.bitSpecs("N4")) ready: pin names not known; wires that end beside it: ready
  // BitLabeledTunnel #(.bitSpecs("N15")) state_15: pin names not known; wires that end beside it: state_15_p1
  // BitLabeledTunnel #(.bitSpecs("N13"), .\output ("true")) N13: pin names not known; wires that end beside it: N13_p1
  Register #(.width(1), .trigger("falling"), .resetType("syncReset")) auto_94 (
    .D(N13_p1), .en(auto_96_y), .Q(state_15_p1), .clk(clk), .clr(auto_89_y));
  Register #(.width(2), .trigger("falling"), .resetType("syncReset"), .resetValue(2)) auto_91 (
    .D(N8_9_p1), .en(auto_93_y), .Q(auto_91_q), .clk(clk), .clr(start_2_p1));
  // BitLabeledTunnel #(.width(2), .bitSpecs("N8,N9"), .\output ("true")) N8_9: pin names not known; wires that end beside it: N8_9_p1
  // BitLabeledTunnel #(.width(2), .bitSpecs("N11,N12")) state_11_12: pin names not known; wires that end beside it: auto_91_q
  // BitLabeledTunnel #(.bitSpecs("N3"), .\output ("true")) start_2: pin names not known; wires that end beside it: start_2_p1
  // BitLabeledTunnel #(.width(3), .bitSpecs("N11,N12,N15"), .\output ("true")) state: pin names not known; wires that end beside it: state_p1
  // BitLabeledTunnel #(.width(2), .bitSpecs("N3,N4"), .\output ("true")) N3_4: pin names not known; wires that end beside it: N3_4_p1
  // BitLabeledTunnel #(.width(3), .bitSpecs("N4,N17,N18"), .\output ("true")) N4_17_18: pin names not known; wires that end beside it: N4_17_18_p1
  Comparator #(.width(3), .mode("unsigned")) comparator_1 (
    .a(state_p1), .b(3'b100), .eq(comparator_1_eq));  // open: gt, lt
  ys_reduce_or_W2 auto_89 (.A(N3_4_p1), .Y(auto_89_y));
  ys_reduce_bool_W3 auto_93 (.A(N4_17_18_p1), .Y(auto_93_y));
  // BitLabeledTunnel #(.bitSpecs("N17"), .\output ("true")) N17: pin names not known; wires that end beside it: N17_p1
  // BitLabeledTunnel #(.width(3), .bitSpecs("N11,N12,N15"), .\output ("true")) state_2: pin names not known; wires that end beside it: state_2_p1
  // BitLabeledTunnel #(.width(2), .bitSpecs("N17,N18"), .\output ("true")) N17_18: pin names not known; wires that end beside it: N17_18_p1
  // BitLabeledTunnel #(.bitSpecs("N18"), .\output ("true")) N18: pin names not known; wires that end beside it: N18_p1
  // BitLabeledTunnel #(.bitSpecs("N17"), .\output ("true")) N17_2: pin names not known; wires that end beside it: N17_2_p1
  // BitLabeledTunnel #(.width(3), .bitSpecs("N24,N25,N13")) N13_24_25: pin names not known; wires that end beside it: N13_24_25_p1
  Multiplexer #(.width(3), .enable("false")) multiplexer_1 (
    .in0(multiplexer_5_out), .in1(3'b100), .out(N13_24_25_p1), .sel(N17_p1));
  // BitLabeledTunnel #(.bitSpecs("N17")) N17_3: pin names not known; wires that end beside it: N17_3_p1
  Comparator #(.width(3), .mode("unsigned")) comparator_2 (.a(state_2_p1), .b(3'b010), .eq(N17_3_p1));  // open: gt, lt
  // BitLabeledTunnel #(.bitSpecs("N18")) N18_2: pin names not known; wires that end beside it: N18_2_p1
  // Logical_AND_Gate #(.width(1)) logical_and_1: pin names not known; wires that end beside it: comparator_1_eq, mul_rdy, N18_2_p1
  ys_reduce_bool_W2 auto_96 (.A(N17_18_p1), .Y(auto_96_y));
  Multiplexer #(.enable("false")) multiplexer_2 (.in0(1'b0), .in1(1'b1), .out(multiplexer_2_out), .sel(N18_p1));
  Multiplexer #(.enable("false")) multiplexer_3 (.in0(1'b0), .in1(1'b1), .out(multiplexer_3_out), .sel(N17_2_p1));
  // BitLabeledTunnel #(.width(3), .bitSpecs("N24,N25,N13"), .\output ("true")) N13_24_25_2: pin names not known; wires that end beside it: N13_24_25_2_p1
  Multiplexer #(.width(3), .enable("false")) multiplexer_4 (
    .in0(N13_24_25_2_p1), .in1(3'b001), .out(multiplexer_4_out), .sel(ready_2_p1));
  // BitLabeledTunnel #(.width(3), .bitSpecs("N8,N9,N28")) N8_9_28: pin names not known; wires that end beside it: multiplexer_4_out
  // BitLabeledTunnel #(.bitSpecs("N4"), .\output ("true")) ready_2: pin names not known; wires that end beside it: ready_2_p1
  // BitLabeledTunnel #(.width(3), .bitSpecs("x,x,x"), .\output ("true")) X_UNDEF_3_9918: pin names not known; wires that end beside it: X_UNDEF_3_9918_p1
  Multiplexer #(.width(3), .enable("false")) multiplexer_5 (
    .in0(X_UNDEF_3_9918_p1), .in1(3'b010), .out(multiplexer_5_out), .sel(N18_3_p1));
  // BitLabeledTunnel #(.bitSpecs("N18"), .\output ("true")) N18_3: pin names not known; wires that end beside it: N18_3_p1
  Multiplexer #(.enable("false")) multiplexer_6 (
    .in0(multiplexer_2_out), .in1(1'b0), .out(multiplexer_6_out), .sel(N17_4_p1));
  // BitLabeledTunnel #(.bitSpecs("N17"), .\output ("true")) N17_4: pin names not known; wires that end beside it: N17_4_p1
  Multiplexer #(.enable("false")) multiplexer_7 (
    .in0(multiplexer_3_out), .in1(1'b0), .out(multiplexer_7_out), .sel(ready_3_p1));
  // BitLabeledTunnel #(.bitSpecs("N4"), .\output ("true")) ready_3: pin names not known; wires that end beside it: ready_3_p1
  // BitLabeledTunnel #(.bitSpecs("N4"), .\output ("true")) ready_4: pin names not known; wires that end beside it: ready_4_p1
  // BitLabeledTunnel #(.bitSpecs("N3"), .\output ("true")) start_3: pin names not known; wires that end beside it: start_3_p1
  Multiplexer #(.enable("false")) multiplexer_8 (
    .in0(multiplexer_6_out), .in1(1'b0), .out(multiplexer_8_out), .sel(ready_4_p1));
  Multiplexer #(.enable("false")) multiplexer_9 (
    .in0(multiplexer_7_out), .in1(1'b0), .out(mul_start), .sel(start_3_p1));
  Multiplexer #(.enable("false")) multiplexer_10 (.in0(multiplexer_8_out), .in1(1'b1), .out(store), .sel(start_4_p1));
  // BitLabeledTunnel #(.bitSpecs("N3"), .\output ("true")) start_4: pin names not known; wires that end beside it: start_4_p1
endmodule

module ys_reduce_bool_W3 (
  input  [2:0] A,
  output Y
);

  wire comparator_1_eq;

  Comparator #(.width(3), .mode("unsigned")) comparator_1 (.a(A), .b(3'b000), .eq(comparator_1_eq));  // open: gt, lt
  not ne0 (Y, comparator_1_eq);
endmodule

module ys_reduce_bool_W2 (
  input  [1:0] A,
  output Y
);

  wire comparator_1_eq;

  not ne0 (Y, comparator_1_eq);
  Comparator #(.width(2), .mode("unsigned")) comparator_1 (.a(A), .b(2'b00), .eq(comparator_1_eq));  // open: gt, lt
endmodule

module ys_reduce_or_W2 (
  input  [1:0] A,
  output Y
);

  wire comparator_1_eq;

  Comparator #(.width(2), .mode("unsigned")) comparator_1 (.a(A), .b(2'b00), .eq(comparator_1_eq));  // open: gt, lt
  not ne0 (Y, comparator_1_eq);
endmodule

module serial_multiplier (
  input  clk,
  input  start,
  input  [31:0] x,
  input  [31:0] y,
  output [31:0] z,
  output ready
);

  wire RX_228_p1, RY_165_p1, RY_197_p1, RY_p1, x_4_p1, y_67_p1;
  wire [30:0] auto_15_q, N166_196_p1, N229_259_p1, RX_260_290_p1;
  wire [31:0] _1_b0_RX_228_RX_260_289_p1, adder_1_out, multiplexer_1_out, multiplexer_2_out,
       multiplexer_3_out, RX_p1, RY_198_227_RY_165_1_b0_p1, x_2_p1, y_2_p1;

  // BitLabeledTunnel #(.width(32), .bitSpecs("N4,N5,N6,N7,N8,N9,N10,N11,N12,N13,N14,N15,N16,N17,N18,N19,N20,N21,N22,N23,N24,N25,N26,N27,N28,N29,N30,N31,N32,N33,N34,N35")) x: pin names not known; wires that end beside it: x
  // BitLabeledTunnel #(.width(32), .bitSpecs("N36,N37,N38,N39,N40,N41,N42,N43,N44,N45,N46,N47,N48,N49,N50,N51,N52,N53,N54,N55,N56,N57,N58,N59,N60,N61,N62,N63,N64,N65,N66,N67")) y: pin names not known; wires that end beside it: y
  Adder #(.width(32)) adder_1 (.a(z), .b(multiplexer_2_out), .out(adder_1_out));  // open: cin, cout
  // BitLabeledTunnel #(.bitSpecs("N228")) RX_228: pin names not known; wires that end beside it: RX_228_p1
  // BitLabeledTunnel #(.bitSpecs("N4"), .\output ("true")) x_4: pin names not known; wires that end beside it: x_4_p1
  Register #(.width(1), .trigger("falling"), .resetType("syncReset"), .resetPolarity("rstActiveLow"), .regHasEnable("false")) auto_16 (
    .D(x_4_p1), .Q(RX_228_p1), .clk(clk), .clr(start));  // open: en
  Register #(.width(32), .trigger("falling"), .resetType("syncReset"), .regHasEnable("false")) auto_13 (
    .D(adder_1_out), .Q(z), .clk(clk), .clr(start));  // open: en
  // BitLabeledTunnel #(.width(31), .bitSpecs("N260,N261,N262,N263,N264,N265,N266,N267,N268,N269,N270,N271,N272,N273,N274,N275,N276,N277,N278,N279,N280,N281,N282,N283,N284,N285,N286,N287,N288,N289,N290")) RX_260_290: pin names not known; wires that end beside it: RX_260_290_p1
  Register #(.width(31), .trigger("falling"), .resetType("noReset"), .regHasEnable("false")) auto_17 (
    .D(N229_259_p1), .Q(RX_260_290_p1), .clk(clk));  // open: en, clr
  // BitLabeledTunnel #(.width(31), .bitSpecs("N229,N230,N231,N232,N233,N234,N235,N236,N237,N238,N239,N240,N241,N242,N243,N244,N245,N246,N247,N248,N249,N250,N251,N252,N253,N254,N255,N256,N257,N258,N259"), .\output ("true")) N229_259: pin names not known; wires that end beside it: N229_259_p1
  // BitLabeledTunnel #(.bitSpecs("N165")) RY_165: pin names not known; wires that end beside it: RY_165_p1
  Register #(.width(1), .trigger("falling"), .resetType("syncReset"), .resetPolarity("rstActiveLow"), .regHasEnable("false")) auto_14 (
    .D(y_67_p1), .Q(RY_165_p1), .clk(clk), .clr(start));  // open: en
  // BitLabeledTunnel #(.bitSpecs("N67"), .\output ("true")) y_67: pin names not known; wires that end beside it: y_67_p1
  Register #(.width(31), .trigger("falling"), .resetType("noReset"), .regHasEnable("false")) auto_15 (
    .D(N166_196_p1), .Q(auto_15_q), .clk(clk));  // open: en, clr
  // BitLabeledTunnel #(.width(31), .bitSpecs("N197,N198,N199,N200,N201,N202,N203,N204,N205,N206,N207,N208,N209,N210,N211,N212,N213,N214,N215,N216,N217,N218,N219,N220,N221,N222,N223,N224,N225,N226,N227")) RY_197_227: pin names not known; wires that end beside it: auto_15_q
  // BitLabeledTunnel #(.width(31), .bitSpecs("N166,N167,N168,N169,N170,N171,N172,N173,N174,N175,N176,N177,N178,N179,N180,N181,N182,N183,N184,N185,N186,N187,N188,N189,N190,N191,N192,N193,N194,N195,N196"), .\output ("true")) N166_196: pin names not known; wires that end beside it: N166_196_p1
  // BitLabeledTunnel #(.width(32), .bitSpecs("0,N228,N260,N261,N262,N263,N264,N265,N266,N267,N268,N269,N270,N271,N272,N273,N274,N275,N276,N277,N278,N279,N280,N281,N282,N283,N284,N285,N286,N287,N288,N289"), .\output ("true")) _1_b0_RX_228_RX_260_289: pin names not known; wires that end beside it: _1_b0_RX_228_RX_260_289_p1
  Multiplexer #(.width(32), .enable("false")) multiplexer_1 (
    .in0(_1_b0_RX_228_RX_260_289_p1), .in1(x_2_p1), .out(multiplexer_1_out), .sel(start));
  // BitLabeledTunnel #(.width(32), .bitSpecs("N4,N5,N6,N7,N8,N9,N10,N11,N12,N13,N14,N15,N16,N17,N18,N19,N20,N21,N22,N23,N24,N25,N26,N27,N28,N29,N30,N31,N32,N33,N34,N35"), .\output ("true")) x_2: pin names not known; wires that end beside it: x_2_p1
  Multiplexer #(.width(32), .enable("false")) multiplexer_2 (
    .in0({32{1'b0}}), .in1(RX_p1), .out(multiplexer_2_out), .sel(RY_197_p1));
  // BitLabeledTunnel #(.width(32), .bitSpecs("N228,N260,N261,N262,N263,N264,N265,N266,N267,N268,N269,N270,N271,N272,N273,N274,N275,N276,N277,N278,N279,N280,N281,N282,N283,N284,N285,N286,N287,N288,N289,N290"), .\output ("true")) RX: pin names not known; wires that end beside it: RX_p1
  // BitLabeledTunnel #(.bitSpecs("N197"), .\output ("true")) RY_197: pin names not known; wires that end beside it: RY_197_p1
  // BitLabeledTunnel #(.width(32), .bitSpecs("N198,N199,N200,N201,N202,N203,N204,N205,N206,N207,N208,N209,N210,N211,N212,N213,N214,N215,N216,N217,N218,N219,N220,N221,N222,N223,N224,N225,N226,N227,N165,0"), .\output ("true")) RY_198_227_RY_165_1_b0: pin names not known; wires that end beside it: RY_198_227_RY_165_1_b0_p1
  Multiplexer #(.width(32), .enable("false")) multiplexer_3 (
    .in0(RY_198_227_RY_165_1_b0_p1), .in1(y_2_p1), .out(multiplexer_3_out), .sel(start));
  // BitLabeledTunnel #(.width(32), .bitSpecs("N36,N37,N38,N39,N40,N41,N42,N43,N44,N45,N46,N47,N48,N49,N50,N51,N52,N53,N54,N55,N56,N57,N58,N59,N60,N61,N62,N63,N64,N65,N66,N67"), .\output ("true")) y_2: pin names not known; wires that end beside it: y_2_p1
  // Logical_NOT_Gate #(.width(32)) logical_not_1: pin names not known; wires that end beside it: ready
  // BitLabeledTunnel #(.width(32), .bitSpecs("N197,N198,N199,N200,N201,N202,N203,N204,N205,N206,N207,N208,N209,N210,N211,N212,N213,N214,N215,N216,N217,N218,N219,N220,N221,N222,N223,N224,N225,N226,N227,N165"), .\output ("true")) RY: pin names not known; wires that end beside it: RY_p1, RY_p1
  // BitLabeledTunnel #(.width(32), .bitSpecs("N291,N229,N230,N231,N232,N233,N234,N235,N236,N237,N238,N239,N240,N241,N242,N243,N244,N245,N246,N247,N248,N249,N250,N251,N252,N253,N254,N255,N256,N257,N258,N259")) N229_259_291: pin names not known; wires that end beside it: multiplexer_1_out
  // BitLabeledTunnel #(.width(32), .bitSpecs("N166,N167,N168,N169,N170,N171,N172,N173,N174,N175,N176,N177,N178,N179,N180,N181,N182,N183,N184,N185,N186,N187,N188,N189,N190,N191,N192,N193,N194,N195,N196,N292")) N166_196_292: pin names not known; wires that end beside it: multiplexer_3_out

  // Other names for the same wires on the sheet: RZ[31:0] = z
endmodule

module primegen_imported (
  input  clk,
  input  start,
  input  [7:0] k,
  input  [7:0] num,
  output [8:0] regI,
  output [8:0] regJ,
  output rdy,
  output p
);

  wire comparator_1_gt, comparator_3_eq, comparator_5_eq, logical_not_1_p1, mg_rdy_2_p1, multiplexer_3_out,
       multiplexer_5_out, multiplexer_8_out, multiplexer_9_out, multiplexer_12_out, multiplexer_13_out,
       N3_122_p1, N38_101_2_p1, N38_116_117_p1, N100_103_p1, N103_p1, N108_127_130_p1, N108_p1, N109, N110,
       N111_118_121_p1, N111_p1, N114_123_126_p1, N114_p1, N115, N120_p1, N121_p1, N125_p1, N126_p1, N129_p1,
       N130_p1, N135, N136, not_prime_p1, or_6_out, procmux_39_CMP0_out, procmux_45_CMP0_out, ram_1_data,
       rdy_2_p1, rdy_p1, start_2_p1, start_3_p1, start_4_p1, X_UNDEF_1_186_p1, X_UNDEF_1_946_p1,
       X_UNDEF_1_9073_p1, X_UNDEF_5_911_p1, X_UNDEF_5_3931_p1, X_UNDEF_5_8567_p1;
  wire [1:0] multiplexer_11_out, N38_101_p1, N118_119_p1, N123_124_p1, N127_128_p1, N131_132, next, state,
       X_UNDEF_2_2763_p1;
  wire [7:0] auto_83_q, N40_47_p1, N140_147_p1;
  wire [8:0] adder_2_out, multiplexer_2_out, N40_48_p1, N58_66_p1, N58_89_p1, N140_147_2_p1,
       regNum_90_97_1_b0_2_p1, regNum_90_97_1_b0_p1;

  // BitLabeledTunnel #(.bitSpecs("N3")) start: pin names not known; wires that end beside it: start
  // BitLabeledTunnel #(.width(9), .bitSpecs("N40,N41,N42,N43,N44,N45,N46,N47,N48"), .\output ("true")) N40_48: pin names not known; wires that end beside it: N40_48_p1
  // BitLabeledTunnel #(.width(9), .bitSpecs("N58,N59,N60,N61,N62,N63,N64,N65,N66,N67,N68,N69,N70,N71,N72,N73,N74,N75,N76,N77,N78,N79,N80,N81,N82,N83,N84,N85,N86,N87,N88,N89")) N58_89: pin names not known; wires that end beside it: N58_89_p1
  Adder #(.width(9)) adder_1 (.a(regI), .b(9'h2), .out(N58_89_p1));  // open: cin, cout
  Adder #(.width(9)) adder_2 (.a(regI), .b(N40_48_p1), .out(adder_2_out));  // open: cin, cout
  // BitLabeledTunnel #(.width(9), .bitSpecs("N58,N59,N60,N61,N62,N63,N64,N65,N66"), .\output ("true")) N58_66: pin names not known; wires that end beside it: N58_66_p1
  Register #(.width(9), .trigger("falling"), .resetType("syncReset"), .resetValue(3)) auto_85 (
    .D(N58_66_p1), .en(multiplexer_12_out), .Q(regI), .clk(clk), .clr(start_3_p1));
  Register #(.trigger("falling"), .resetType("noReset")) auto_83 (
    .D(num), .en(start_2_p1), .Q(auto_83_q), .clk(clk));  // open: clr
  // BitLabeledTunnel #(.width(8), .bitSpecs("N90,N91,N92,N93,N94,N95,N96,N97")) regNum: pin names not known; wires that end beside it: auto_83_q
  // BitLabeledTunnel #(.bitSpecs("N3"), .\output ("true")) start_2: pin names not known; wires that end beside it: start_2_p1
  Register #(.width(9), .trigger("falling"), .resetType("noReset")) auto_86 (
    .D(adder_2_out), .en(or_6_out), .Q(regJ), .clk(clk));  // open: clr
  // BitLabeledTunnel #(.bitSpecs("N3"), .\output ("true")) start_3: pin names not known; wires that end beside it: start_3_p1
  Comparator #(.width(9), .mode("unsigned")) comparator_1 (
    .a(regJ), .b(regNum_90_97_1_b0_p1), .gt(comparator_1_gt));  // open: eq, lt
  // BitLabeledTunnel #(.width(9), .bitSpecs("N90,N91,N92,N93,N94,N95,N96,N97,0"), .\output ("true")) regNum_90_97_1_b0: pin names not known; wires that end beside it: regNum_90_97_1_b0_p1
  // BitLabeledTunnel #(.bitSpecs("x"), .\output ("true")) X_UNDEF_1_186: pin names not known; wires that end beside it: X_UNDEF_1_186_p1
  // BitLabeledTunnel #(.bitSpecs("N108"), .\output ("true")) N108: pin names not known; wires that end beside it: N108_p1
  // BitLabeledTunnel #(.bitSpecs("N103"), .\output ("true")) N103: pin names not known; wires that end beside it: N103_p1
  // BitLabeledTunnel #(.bitSpecs("N100")) mg_rdy: pin names not known; wires that end beside it: comparator_1_gt
  Multiplexer #(.enable("false")) multiplexer_1 (.in0(X_UNDEF_1_186_p1), .in1(N108_p1), .out(N110), .sel(N109));
  or or_6 (or_6_out, multiplexer_8_out, N103_p1);
  // BitLabeledTunnel #(.width(5), .bitSpecs("x,x,x,x,x"), .\output ("true")) X_UNDEF_5_3931: pin names not known; wires that end beside it: X_UNDEF_5_3931_p1, X_UNDEF_5_3931_p1, 10'hc9
  // BitLabeledTunnel #(.width(2), .bitSpecs("N100,N103"), .\output ("true")) N100_103: pin names not known; wires that end beside it: N100_103_p1, N100_103_p1
  // BitLabeledTunnel #(.bitSpecs("N111"), .\output ("true")) N111: pin names not known; wires that end beside it: N111_p1
  // BitLabeledTunnel #(.bitSpecs("N100"), .\output ("true")) mg_rdy_2: pin names not known; wires that end beside it: mg_rdy_2_p1
  not procmux_45_CMP0 (procmux_45_CMP0_out, mg_rdy_2_p1);
  Multiplexer #(.width(9), .enable("false")) multiplexer_2 (
    .in0(regJ), .in1(regI), .out(multiplexer_2_out), .sel(multiplexer_8_out));
  // BitLabeledTunnel #(.width(5), .bitSpecs("N127,N128,N129,N130,N108")) N108_127_130: pin names not known; wires that end beside it: N108_127_130_p1
  // Priority_Multiplexer #(.width(5)) priority_multiplexer_1: pin names not known; wires that end beside it: N108_127_130_p1
  Multiplexer #(.enable("false")) multiplexer_3 (
    .in0(N110), .in1(N111_p1), .out(multiplexer_3_out), .sel(comparator_3_eq));
  // BitLabeledTunnel #(.bitSpecs("N103")) N103_2: pin names not known; wires that end beside it: procmux_45_CMP0_out
  // BitLabeledTunnel #(.width(9), .bitSpecs("N40,N41,N42,N43,N44,N45,N46,N47,N48")) N40_48_2: pin names not known; wires that end beside it: multiplexer_2_out
  Register #(.width(2), .trigger("falling"), .resetType("noReset"), .regHasEnable("false")) procdff_79 (
    .D(next), .Q(state), .clk(clk));  // open: en, clr
  // BitLabeledTunnel #(.width(9), .bitSpecs("N90,N91,N92,N93,N94,N95,N96,N97,0"), .\output ("true")) regNum_90_97_1_b0_2: pin names not known; wires that end beside it: regNum_90_97_1_b0_2_p1
  // BitLabeledTunnel #(.width(8), .bitSpecs("N40,N41,N42,N43,N44,N45,N46,N47"), .\output ("true")) N40_47: pin names not known; wires that end beside it: N40_47_p1
  // BitLabeledTunnel #(.bitSpecs("N101"), .\output ("true")) not_prime: pin names not known; wires that end beside it: not_prime_p1
  // BitLabeledTunnel #(.bitSpecs("x"), .\output ("true")) X_UNDEF_1_9073: pin names not known; wires that end beside it: X_UNDEF_1_9073_p1
  // BitLabeledTunnel #(.bitSpecs("N130"), .\output ("true")) N130: pin names not known; wires that end beside it: N130_p1
  // BitLabeledTunnel #(.bitSpecs("x"), .\output ("true")) X_UNDEF_1_946: pin names not known; wires that end beside it: X_UNDEF_1_946_p1
  // BitLabeledTunnel #(.bitSpecs("N129"), .\output ("true")) N129: pin names not known; wires that end beside it: N129_p1
  // BitLabeledTunnel #(.width(5), .bitSpecs("x,x,x,x,x"), .\output ("true")) X_UNDEF_5_911: pin names not known; wires that end beside it: X_UNDEF_5_911_p1, X_UNDEF_5_911_p1, 15'h4b20
  // BitLabeledTunnel #(.width(2), .bitSpecs("x,x"), .\output ("true")) X_UNDEF_2_2763: pin names not known; wires that end beside it: X_UNDEF_2_2763_p1
  // BitLabeledTunnel #(.width(2), .bitSpecs("N127,N128"), .\output ("true")) N127_128: pin names not known; wires that end beside it: N127_128_p1
  // BitLabeledTunnel #(.bitSpecs("N114"), .\output ("true")) N114: pin names not known; wires that end beside it: N114_p1
  // BitLabeledTunnel #(.bitSpecs("N38")) rdy: pin names not known; wires that end beside it: rdy_p1
  Comparator #(.width(9), .mode("unsigned")) comparator_2 (
    .a(regI), .b(regNum_90_97_1_b0_2_p1), .gt(rdy_p1));  // open: eq, lt
  // BitLabeledTunnel #(.width(8), .bitSpecs("N140,N141,N142,N143,N144,N145,N146,N147")) N140_147: pin names not known; wires that end beside it: N140_147_p1
  Multiplexer #(.width(8), .enable("false")) multiplexer_4 (
    .in0(N40_47_p1), .in1(k), .out(N140_147_p1), .sel(rdy_2_p1));
  // BitLabeledTunnel #(.bitSpecs("N38"), .\output ("true")) rdy_2: pin names not known; wires that end beside it: rdy_2_p1
  not not_2 (p, not_prime_p1);
  Multiplexer #(.enable("false")) multiplexer_5 (
    .in0(X_UNDEF_1_9073_p1), .in1(N130_p1), .out(multiplexer_5_out), .sel(N109));
  Multiplexer #(.enable("false")) multiplexer_6 (.in0(X_UNDEF_1_946_p1), .in1(N129_p1), .out(N135), .sel(N109));
  // BitLabeledTunnel #(.width(5), .bitSpecs("N118,N119,N120,N121,N111")) N111_118_121: pin names not known; wires that end beside it: N111_118_121_p1
  // Priority_Multiplexer #(.width(5), .swidth(3)) priority_multiplexer_2: pin names not known; wires that end beside it: N111_118_121_p1
  // BitLabeledTunnel #(.width(3), .bitSpecs("N38,N116,N117"), .\output ("true")) N38_116_117: pin names not known; wires that end beside it: N38_116_117_p1, N38_116_117_p1
  Multiplexer #(.width(2), .enable("false")) multiplexer_7 (
    .in0(X_UNDEF_2_2763_p1), .in1(N127_128_p1), .out(N131_132), .sel(N109));
  Multiplexer #(.enable("false")) multiplexer_8 (
    .in0(multiplexer_3_out), .in1(N114_p1), .out(multiplexer_8_out), .sel(N115));
  Comparator #(.width(2), .mode("unsigned")) comparator_3 (.a(state), .b(2'b01), .eq(comparator_3_eq));  // open: gt, lt
  Comparator #(.width(2), .mode("unsigned")) comparator_4 (.a(state), .b(2'b10), .eq(N109));  // open: gt, lt
  // BitLabeledTunnel #(.width(2), .bitSpecs("N101,N38"), .\output ("true")) N38_101: pin names not known; wires that end beside it: N38_101_p1
  // BitLabeledTunnel #(.width(5), .bitSpecs("x,x,x,x,x"), .\output ("true")) X_UNDEF_5_8567: pin names not known; wires that end beside it: X_UNDEF_5_8567_p1, X_UNDEF_5_8567_p1, 10'h9
  // Logical_NOT_Gate #(.width(2)) logical_not_1: pin names not known; wires that end beside it: logical_not_1_p1
  // BitLabeledTunnel #(.bitSpecs("N117")) N117: pin names not known; wires that end beside it: logical_not_1_p1
  // BitLabeledTunnel #(.width(2), .bitSpecs("N101,N38"), .\output ("true")) N38_101_2: pin names not known; wires that end beside it: N38_101_2_p1, N38_101_2_p1
  Comparator #(.width(2), .mode("unsigned")) comparator_5 (
    .a(N38_101_p1), .b(2'b01), .eq(comparator_5_eq));  // open: gt, lt
  // BitLabeledTunnel #(.bitSpecs("N116")) N116: pin names not known; wires that end beside it: comparator_5_eq
  // BitLabeledTunnel #(.width(5), .bitSpecs("N123,N124,N125,N126,N114")) N114_123_126: pin names not known; wires that end beside it: N114_123_126_p1
  // Priority_Multiplexer #(.width(5)) priority_multiplexer_3: pin names not known; wires that end beside it: N114_123_126_p1
  // BitLabeledTunnel #(.width(2), .bitSpecs("N3,N122"), .\output ("true")) N3_122: pin names not known; wires that end beside it: N3_122_p1, N3_122_p1
  Multiplexer #(.enable("false")) multiplexer_9 (
    .in0(multiplexer_5_out), .in1(N121_p1), .out(multiplexer_9_out), .sel(comparator_3_eq));
  // BitLabeledTunnel #(.bitSpecs("N121"), .\output ("true")) N121: pin names not known; wires that end beside it: N121_p1
  Multiplexer #(.enable("false")) multiplexer_10 (.in0(N135), .in1(N120_p1), .out(N136), .sel(comparator_3_eq));
  // BitLabeledTunnel #(.bitSpecs("N120"), .\output ("true")) N120: pin names not known; wires that end beside it: N120_p1
  Multiplexer #(.width(2), .enable("false")) multiplexer_11 (
    .in0(N131_132), .in1(N118_119_p1), .out(multiplexer_11_out), .sel(comparator_3_eq));
  // BitLabeledTunnel #(.width(2), .bitSpecs("N118,N119"), .\output ("true")) N118_119: pin names not known; wires that end beside it: N118_119_p1
  // Logical_NOT_Gate #(.width(2)) logical_not_2: pin names not known; wires that end beside it: state, N115
  // BitLabeledTunnel #(.bitSpecs("N3"), .\output ("true")) start_4: pin names not known; wires that end beside it: start_4_p1
  not procmux_39_CMP0 (procmux_39_CMP0_out, start_4_p1);
  Multiplexer #(.enable("false")) multiplexer_12 (
    .in0(multiplexer_9_out), .in1(N126_p1), .out(multiplexer_12_out), .sel(N115));
  // BitLabeledTunnel #(.bitSpecs("N126"), .\output ("true")) N126: pin names not known; wires that end beside it: N126_p1
  Multiplexer #(.enable("false")) multiplexer_13 (.in0(N136), .in1(N125_p1), .out(multiplexer_13_out), .sel(N115));
  // BitLabeledTunnel #(.bitSpecs("N125"), .\output ("true")) N125: pin names not known; wires that end beside it: N125_p1
  Multiplexer #(.width(2), .enable("false")) multiplexer_14 (
    .in0(multiplexer_11_out), .in1(N123_124_p1), .out(next), .sel(N115));
  // BitLabeledTunnel #(.width(2), .bitSpecs("N123,N124"), .\output ("true")) N123_124: pin names not known; wires that end beside it: N123_124_p1
  // BitLabeledTunnel #(.bitSpecs("N122")) N122: pin names not known; wires that end beside it: procmux_39_CMP0_out
  // BitLabeledTunnel #(.width(9), .bitSpecs("N140,N141,N142,N143,N144,N145,N146,N147,0"), .\output ("true")) N140_147_2: pin names not known; wires that end beside it: N140_147_2_p1
  RAM #(.addrWidth(9), .dataWidth(1), .bus("separate")) ram_1 (
    .addr(N140_147_2_p1), .din(1'b1), .data(ram_1_data), .str(multiplexer_13_out), .clk(clk));  // open: sel, ld, clr
  // BitLabeledTunnel #(.bitSpecs("N101")) not_prime_2: pin names not known; wires that end beside it: ram_1_data
  // BitLabeledTunnel #(.bitSpecs("N38"), .\output ("true")) rdy_3: pin names not known; wires that end beside it: rdy
endmodule

module factorial_imported_v1 (
  input  clk,
  input  start,
  input  [7:0] n,
  output [31:0] f,
  output ready
);

  wire ctrl_mul_start, mul_ready, store;
  wire [7:0] multiplexer_2_out, multiplexer_4_out, procdff_10_q, RN_2_p1, RN_4_p1, RN_p1, subtractor_1_out;
  wire [31:0] multiplexer_3_out, N61_92, RF, RN_45_52_24_b0_p1;

  // BitLabeledTunnel #(.width(8), .bitSpecs("N45,N46,N47,N48,N49,N50,N51,N52"), .\output ("true")) RN: pin names not known; wires that end beside it: RN_p1
  Comparator #(.mode("unsigned")) comparator_1 (.a(RN_p1), .b(8'h1), .lt(ready));  // open: gt, eq
  Register #(.width(32), .trigger("falling"), .resetType("noReset"), .regHasEnable("false")) procdff_11 (
    .D(N61_92), .Q(RF), .clk(clk));  // open: en, clr
  // BitLabeledTunnel #(.width(8), .bitSpecs("N45,N46,N47,N48,N49,N50,N51,N52"), .\output ("true")) RN_2: pin names not known; wires that end beside it: RN_2_p1
  Subtractor subtractor_1 (.a(RN_2_p1), .b(8'h1), .out(subtractor_1_out));  // open: bin, bout
  Register #(.trigger("falling"), .resetType("noReset"), .regHasEnable("false")) procdff_10 (
    .D(multiplexer_2_out), .Q(procdff_10_q), .clk(clk));  // open: en, clr
  // BitLabeledTunnel #(.width(8), .bitSpecs("N45,N46,N47,N48,N49,N50,N51,N52")) RN_3: pin names not known; wires that end beside it: procdff_10_q
  Multiplexer #(.width(32), .enable("false")) multiplexer_1 (
    .in0(RF), .in1(multiplexer_3_out), .out(N61_92), .sel(store));
  // BitLabeledTunnel #(.width(8), .bitSpecs("N45,N46,N47,N48,N49,N50,N51,N52"), .\output ("true")) RN_4: pin names not known; wires that end beside it: RN_4_p1
  Multiplexer #(.width(8), .enable("false")) multiplexer_2 (
    .in0(RN_4_p1), .in1(multiplexer_4_out), .out(multiplexer_2_out), .sel(store));
  ctrl ctrl (.clk(clk), .start(start), .ready(ready), .mul_rdy(mul_ready), .store(store), .mul_start(ctrl_mul_start));
  Multiplexer #(.width(32), .enable("false")) multiplexer_3 (
    .in0(f), .in1(32'h1), .out(multiplexer_3_out), .sel(start));
  // BitLabeledTunnel #(.width(32), .bitSpecs("N45,N46,N47,N48,N49,N50,N51,N52,0,0,0,0,0,0,0,0,0,0,0,0,0,0,0,0,0,0,0,0,0,0,0,0"), .\output ("true")) RN_45_52_24_b0: pin names not known; wires that end beside it: RN_45_52_24_b0_p1
  Multiplexer #(.width(8), .enable("false")) multiplexer_4 (
    .in0(subtractor_1_out), .in1(n), .out(multiplexer_4_out), .sel(start));
  serial_multiplier mul (.clk(clk), .start(ctrl_mul_start), .x(RN_45_52_24_b0_p1), .y(RF), .z(f), .ready(mul_ready));
endmodule
