// Logisim project folding.circ as structural Verilog
module folding (
  input  a,
  input  b,
  input  c,
  input  d,
  output x
);

  // BitLabeledTunnel #(.bitSpecs("N2")) a: pin names not known; wires that end beside it: a
  // BitLabeledTunnel #(.bitSpecs("N3")) b: pin names not known; wires that end beside it: b
  // BitLabeledTunnel #(.bitSpecs("N4")) c: pin names not known; wires that end beside it: c
  // BitLabeledTunnel #(.bitSpecs("N5")) d: pin names not known; wires that end beside it: d

  assign x = 1'b0;
endmodule
