// Logisim project palindrome.circ as structural Verilog
module p2 (
  input  clk,
  input  start,
  input  [31:0] x,
  output rdy,
  output isp
);

  wire i_53_57_27_b0_p1, j_38_42_27_b0_p1, logical_not_1_p2, N66;
  wire [3:0] dynamic_shifter_1_p1, dynamic_shifter_2_p1;
  wire [4:0] adder_1_out, auto_28_q, i_2_p1, i_3_p1, i_p1, j_3_p1, j_p1, N48_52;

  // BitLabeledTunnel #(.width(5), .bitSpecs("N38,N39,N40,N41,N42"), .\output ("true")) j: pin names not known; wires that end beside it: j_p1
  Adder #(.width(5)) adder_1 (.a(j_p1), .b(5'b00100), .out(adder_1_out));  // open: cin, cout
  Comparator #(.width(4), .mode("unsigned")) comparator_1 (
    .a(dynamic_shifter_2_p1), .b(dynamic_shifter_1_p1), .eq(isp));  // open: gt, lt
  Register #(.width(5), .trigger("falling"), .resetType("syncReset"), .enablePolarity("enActiveLow")) auto_28 (
    .D(adder_1_out), .en(rdy), .Q(auto_28_q), .clk(clk), .clr(start));
  // BitLabeledTunnel #(.width(5), .bitSpecs("N38,N39,N40,N41,N42")) j_2: pin names not known; wires that end beside it: auto_28_q
  // BitLabeledTunnel #(.width(5), .bitSpecs("N53,N54,N55,N56,N57")) i: pin names not known; wires that end beside it: i_p1
  Register #(.width(5), .trigger("falling"), .resetType("syncReset"), .resetValue(28), .enablePolarity("enActiveLow")) auto_26 (
    .D(N48_52), .en(rdy), .Q(i_p1), .clk(clk), .clr(start));
  // Logical_NOT_Gate #(.width(1)) logical_not_1: pin names not known; wires that end beside it: isp, logical_not_1_p2
  // Dynamic_Shifter #(.aWidth(32), .bWidth(32), .yWidth(4), .mode("shiftx"), .bSigned("true")) dynamic_shifter_1: pin names not known; wires that end beside it: dynamic_shifter_1_p1
  // BitLabeledTunnel #(.width(32), .bitSpecs("N38,N39,N40,N41,N42,0,0,0,0,0,0,0,0,0,0,0,0,0,0,0,0,0,0,0,0,0,0,0,0,0,0,0"), .\output ("true")) j_38_42_27_b0: pin names not known; wires that end beside it: j_38_42_27_b0_p1, x, j_38_42_27_b0_p1
  // Dynamic_Shifter #(.aWidth(32), .bWidth(32), .yWidth(4), .mode("shiftx"), .bSigned("true")) dynamic_shifter_2: pin names not known; wires that end beside it: dynamic_shifter_2_p1
  // BitLabeledTunnel #(.width(32), .bitSpecs("N53,N54,N55,N56,N57,0,0,0,0,0,0,0,0,0,0,0,0,0,0,0,0,0,0,0,0,0,0,0,0,0,0,0"), .\output ("true")) i_53_57_27_b0: pin names not known; wires that end beside it: i_53_57_27_b0_p1, x, i_53_57_27_b0_p1
  // BitLabeledTunnel #(.width(5), .bitSpecs("N53,N54,N55,N56,N57"), .\output ("true")) i_2: pin names not known; wires that end beside it: i_2_p1
  ys_le_____W5_W5 le_6 (.A(i_2_p1), .B(j_3_p1), .Y(N66));
  // BitLabeledTunnel #(.width(5), .bitSpecs("N38,N39,N40,N41,N42"), .\output ("true")) j_3: pin names not known; wires that end beside it: j_3_p1
  // BitLabeledTunnel #(.width(5), .bitSpecs("N53,N54,N55,N56,N57"), .\output ("true")) i_3: pin names not known; wires that end beside it: i_3_p1
  Subtractor #(.width(5)) subtractor_1 (.a(i_3_p1), .b(5'b00100), .out(N48_52));  // open: bin, bout
  // Logical_OR_Gate #(.width(1)) logical_or_1: pin names not known; wires that end beside it: N66, logical_not_1_p2, rdy
endmodule

module ys_le_____W5_W5 (
  input  [4:0] A,
  input  [4:0] B,
  output Y
);

  wire comparator_1_gt;

  Comparator #(.width(5), .mode("unsigned")) comparator_1 (.a(A), .b(B), .gt(comparator_1_gt));  // open: eq, lt
  not NE (Y, comparator_1_gt);
endmodule
