// Logisim project ram.circ as structural Verilog
module ram (
  input  clk,
  input  str,
  input  [3:0] addr,
  input  [7:0] x,
  output [7:0] data
);

  wire N24;
  wire [3:0] N33_36_p1, X_UNDEF_4_8359_p1;
  wire [7:0] N25_32, X_UNDEF_8_6627_p1;

  // BitLabeledTunnel #(.width(4), .bitSpecs("x,x,x,x"), .\output ("true")) X_UNDEF_4_8359: pin names not known; wires that end beside it: X_UNDEF_4_8359_p1
  // BitLabeledTunnel #(.width(8), .bitSpecs("x,x,x,x,x,x,x,x"), .\output ("true")) X_UNDEF_8_6627: pin names not known; wires that end beside it: X_UNDEF_8_6627_p1
  // BitLabeledTunnel #(.width(4), .bitSpecs("N33,N34,N35,N36")) N33_36: pin names not known; wires that end beside it: N33_36_p1
  Multiplexer #(.width(4), .enable("false")) multiplexer_1 (
    .in0(X_UNDEF_4_8359_p1), .in1(addr), .out(N33_36_p1), .sel(str));
  Multiplexer #(.width(8), .enable("false")) multiplexer_2 (.in0(X_UNDEF_8_6627_p1), .in1(x), .out(N25_32), .sel(str));
  print display_29 (.EN(N24), .TRG(clk));
  RAM #(.addrWidth(4), .bus("separate"), .trigger("falling")) ram_1 (
    .addr(addr), .din(N25_32), .data(data), .str(N24), .clk(clk), .ld(1'b1));  // open: sel, clr
  Multiplexer #(.enable("false")) multiplexer_3 (.in0(1'b0), .in1(1'b1), .out(N24), .sel(str));
endmodule

module print (
  input  EN,
  input  TRG
);
endmodule
