// Logisim project ram_search.circ as structural Verilog
module ram_search (
  input  clk,
  input  add,
  input  start,
  input  reset,
  input  [7:0] x,
  output rdy,
  output found
);

  wire logical_not_1_p2, N36_p1, N37, N54, or_7_out, start_2_p1, start_3_p1;
  wire [1:0] N4_36_p1;
  wire [3:0] address, multiplexer_2_out, N20_23, N28_31, regCnt, regNxt;
  wire [7:0] auto_35_q, ram_1_data;

  // BitLabeledTunnel #(.bitSpecs("N4")) start: pin names not known; wires that end beside it: start
  Adder #(.width(4)) adder_1 (.a(regCnt), .b(4'b0001), .out(N20_23));  // open: cin, cout
  Adder #(.width(4)) adder_2 (.a(regNxt), .b(4'b0001), .out(N28_31));  // open: cin, cout
  // BitLabeledTunnel #(.bitSpecs("N36"), .\output ("true")) N36: pin names not known; wires that end beside it: N36_p1
  Register #(.trigger("falling"), .resetType("syncReset")) auto_35 (
    .D(x), .en(N37), .Q(auto_35_q), .clk(clk), .clr(reset));
  Register #(.width(4), .trigger("falling"), .resetType("syncReset")) auto_31 (
    .D(multiplexer_2_out), .en(N36_p1), .Q(regCnt), .clk(clk), .clr(reset));
  Register #(.width(4), .trigger("falling"), .resetType("syncReset")) auto_33 (
    .D(N28_31), .en(add), .Q(regNxt), .clk(clk), .clr(reset));
  Comparator #(.width(4), .mode("unsigned")) comparator_1 (.a(regCnt), .b(regNxt), .eq(N54));  // open: gt, lt
  Multiplexer #(.width(4), .enable("false")) multiplexer_1 (.in0(regCnt), .in1(regNxt), .out(address), .sel(add));
  // Logical_NOT_Gate #(.width(1)) logical_not_1: pin names not known; wires that end beside it: rdy, logical_not_1_p2
  // BitLabeledTunnel #(.width(2), .bitSpecs("N4,N36"), .\output ("true")) N4_36: pin names not known; wires that end beside it: N4_36_p1
  // BitLabeledTunnel #(.bitSpecs("N4"), .\output ("true")) start_2: pin names not known; wires that end beside it: start_2_p1
  ys_reduce_and_W2 auto_37 (.A(N4_36_p1), .Y(N37));
  Comparator #(.mode("unsigned")) comparator_2 (.a(ram_1_data), .b(auto_35_q), .eq(found));  // open: gt, lt
  Multiplexer #(.width(4), .enable("false")) multiplexer_2 (
    .in0(N20_23), .in1(4'b0000), .out(multiplexer_2_out), .sel(start_3_p1));
  // BitLabeledTunnel #(.bitSpecs("N4"), .\output ("true")) start_3: pin names not known; wires that end beside it: start_3_p1
  or or_7 (or_7_out, start_2_p1, logical_not_1_p2);
  // BitLabeledTunnel #(.bitSpecs("N36")) N36_2: pin names not known; wires that end beside it: or_7_out
  or or_3 (rdy, found, N54);
  RAM #(.addrWidth(4), .bus("separate")) ram_1 (
    .addr(address), .din(x), .data(ram_1_data), .str(add), .clk(clk));  // open: sel, ld, clr
endmodule

module ys_reduce_and_W2 (
  input  [1:0] A,
  output Y
);

  Comparator #(.width(2), .mode("unsigned")) comparator_1 (.a(A), .b(2'b11), .eq(Y));  // open: gt, lt
endmodule
