// Logisim project rom.circ as structural Verilog
module rom (
  input  [7:0] addr,
  output [7:0] data
);

  wire comparator_2_eq, comparator_5_eq, N18_23_p4, N20_p1, N21_p1, N22_p1, N23_p1;

  // Priority_Multiplexer #(.swidth(6)) priority_multiplexer_1: pin names not known; wires that end beside it: data
  // BitLabeledTunnel #(.width(6), .bitSpecs("N18,N19,N20,N21,N22,N23"), .\output ("true")) N18_23: pin names not known; wires that end beside it: {8{1'b0}}, 32'h5070b0d, 16'h203, N18_23_p4, N18_23_p4
  // BitLabeledTunnel #(.bitSpecs("N20")) N20: pin names not known; wires that end beside it: N20_p1
  Comparator #(.mode("unsigned")) comparator_1 (.a(addr), .b(8'h3), .eq(N20_p1));  // open: gt, lt
  Comparator #(.mode("unsigned")) comparator_2 (.a(addr), .b(8'h4), .eq(comparator_2_eq));  // open: gt, lt
  // BitLabeledTunnel #(.bitSpecs("N19")) N19: pin names not known; wires that end beside it: comparator_2_eq
  // BitLabeledTunnel #(.bitSpecs("N22")) N22: pin names not known; wires that end beside it: N22_p1
  Comparator #(.mode("unsigned")) comparator_3 (.a(addr), .b(8'h1), .eq(N22_p1));  // open: gt, lt
  // BitLabeledTunnel #(.bitSpecs("N23")) N23: pin names not known; wires that end beside it: N23_p1
  // Logical_NOT_Gate logical_not_1: pin names not known; wires that end beside it: addr, N23_p1
  // BitLabeledTunnel #(.bitSpecs("N21")) N21: pin names not known; wires that end beside it: N21_p1
  Comparator #(.mode("unsigned")) comparator_4 (.a(addr), .b(8'h2), .eq(N21_p1));  // open: gt, lt
  Comparator #(.mode("unsigned")) comparator_5 (.a(addr), .b(8'h5), .eq(comparator_5_eq));  // open: gt, lt
  // BitLabeledTunnel #(.bitSpecs("N18")) N18: pin names not known; wires that end beside it: comparator_5_eq
endmodule
