// Logisim project rom_search.circ as structural Verilog
module rom_search (
  input  clk,
  input  start,
  input  reset,
  input  [7:0] x,
  output rdy,
  output found
);

  wire carry_p1, logical_or_2_p1, N28_p1, N29, N46, start_2_p1, start_3_p1;
  wire [1:0] N3_28_p1;
  wire [3:0] incCnt_p1, multiplexer_1_out, regCnt_p1;
  wire [4:0] N19_23_p1, regCnt_15_18_1_b0_p1;
  wire [7:0] regCnt_15_18_4_b0_p1, regX, rom_1_data;

  // BitLabeledTunnel #(.bitSpecs("N3")) start: pin names not known; wires that end beside it: start
  // BitLabeledTunnel #(.width(5), .bitSpecs("N15,N16,N17,N18,0"), .\output ("true")) regCnt_15_18_1_b0: pin names not known; wires that end beside it: regCnt_15_18_1_b0_p1
  // BitLabeledTunnel #(.width(5), .bitSpecs("N19,N20,N21,N22,N23")) N19_23: pin names not known; wires that end beside it: N19_23_p1
  Adder #(.width(5)) adder_1 (.a(regCnt_15_18_1_b0_p1), .b(5'b00001), .out(N19_23_p1));  // open: cin, cout
  // Logical_OR_Gate #(.width(1)) logical_or_1: pin names not known; wires that end beside it: rdy
  // BitLabeledTunnel #(.bitSpecs("N23"), .\output ("true")) carry: pin names not known; wires that end beside it: carry_p1, found, carry_p1
  // BitLabeledTunnel #(.bitSpecs("N28"), .\output ("true")) N28: pin names not known; wires that end beside it: N28_p1
  // Logical_NOT_Gate #(.width(1)) logical_not_1: pin names not known; wires that end beside it: rdy, N46
  Register #(.trigger("falling")) auto_16 (.D(x), .en(N29), .Q(regX), .clk(clk), .clr(reset));
  // BitLabeledTunnel #(.width(4), .bitSpecs("N15,N16,N17,N18")) regCnt: pin names not known; wires that end beside it: regCnt_p1
  Register #(.width(4), .trigger("falling")) auto_15 (
    .D(multiplexer_1_out), .en(N28_p1), .Q(regCnt_p1), .clk(clk), .clr(reset));
  Comparator #(.mode("unsigned")) comparator_1 (.a(rom_1_data), .b(regX), .eq(found));  // open: gt, lt
  // BitLabeledTunnel #(.bitSpecs("N3"), .\output ("true")) start_2: pin names not known; wires that end beside it: start_2_p1, start_2_p1, N46
  // Logical_OR_Gate #(.width(1)) logical_or_2: pin names not known; wires that end beside it: logical_or_2_p1
  // BitLabeledTunnel #(.width(2), .bitSpecs("N3,N28"), .\output ("true")) N3_28: pin names not known; wires that end beside it: N3_28_p1
  ys_reduce_and_W2 auto_18 (.A(N3_28_p1), .Y(N29));
  // BitLabeledTunnel #(.width(4), .bitSpecs("N19,N20,N21,N22"), .\output ("true")) incCnt: pin names not known; wires that end beside it: incCnt_p1
  Multiplexer #(.width(4), .enable("false")) multiplexer_1 (
    .in0(incCnt_p1), .in1(4'b0000), .out(multiplexer_1_out), .sel(start_3_p1));
  // BitLabeledTunnel #(.bitSpecs("N3"), .\output ("true")) start_3: pin names not known; wires that end beside it: start_3_p1
  // BitLabeledTunnel #(.bitSpecs("N28")) N28_2: pin names not known; wires that end beside it: logical_or_2_p1
  // BitLabeledTunnel #(.width(8), .bitSpecs("N15,N16,N17,N18,0,0,0,0"), .\output ("true")) regCnt_15_18_4_b0: pin names not known; wires that end beside it: regCnt_15_18_4_b0_p1
  ROM rom_1 (.addr(regCnt_15_18_4_b0_p1), .data(rom_1_data));
endmodule

module ys_reduce_and_W2 (
  input  [1:0] A,
  output Y
);

  Comparator #(.width(2), .mode("unsigned")) comparator_1 (.a(A), .b(2'b11), .eq(Y));  // open: gt, lt
endmodule
