// Logisim project seq1s.circ as structural Verilog
module p1 (
  input  clk,
  input  start,
  input  [31:0] x,
  output rdy,
  output [5:0] z
);

  wire N113, N114, XReg_2_p1;
  wire [5:0] N43_48;
  wire [31:0] _1_b0_XReg_49_79_p1, N81_112, N115_146, procdff_17_q, XReg_p1;

  // BitLabeledTunnel #(.width(32), .bitSpecs("0,N49,N50,N51,N52,N53,N54,N55,N56,N57,N58,N59,N60,N61,N62,N63,N64,N65,N66,N67,N68,N69,N70,N71,N72,N73,N74,N75,N76,N77,N78,N79"), .\output ("true")) _1_b0_XReg_49_79: pin names not known; wires that end beside it: _1_b0_XReg_49_79_p1
  // BitLabeledTunnel #(.width(32), .bitSpecs("N49,N50,N51,N52,N53,N54,N55,N56,N57,N58,N59,N60,N61,N62,N63,N64,N65,N66,N67,N68,N69,N70,N71,N72,N73,N74,N75,N76,N77,N78,N79,N80"), .\output ("true")) XReg: pin names not known; wires that end beside it: XReg_p1
  assign N81_112 = _1_b0_XReg_49_79_p1 & XReg_p1;  // AND_Gate and_4, 32 bits wide
  Adder #(.width(6)) adder_1 (.a(z), .b(6'b000001), .out(N43_48));  // open: cin, cout
  // Logical_NOT_Gate #(.width(32)) logical_not_1: pin names not known; wires that end beside it: rdy
  // BitLabeledTunnel #(.width(32), .bitSpecs("N49,N50,N51,N52,N53,N54,N55,N56,N57,N58,N59,N60,N61,N62,N63,N64,N65,N66,N67,N68,N69,N70,N71,N72,N73,N74,N75,N76,N77,N78,N79,N80"), .\output ("true")) XReg_2: pin names not known; wires that end beside it: XReg_2_p1, XReg_2_p1
  Register #(.width(32), .trigger("falling"), .resetType("noReset"), .regHasEnable("false")) procdff_17 (
    .D(N115_146), .Q(procdff_17_q), .clk(clk));  // open: en, clr
  Register #(.width(6), .trigger("falling"), .resetType("syncReset")) auto_19 (
    .D(N43_48), .en(N113), .Q(z), .clk(clk), .clr(start));
  // BitLabeledTunnel #(.width(32), .bitSpecs("N49,N50,N51,N52,N53,N54,N55,N56,N57,N58,N59,N60,N61,N62,N63,N64,N65,N66,N67,N68,N69,N70,N71,N72,N73,N74,N75,N76,N77,N78,N79,N80")) XReg_3: pin names not known; wires that end beside it: procdff_17_q
  // Logical_NOT_Gate #(.width(1)) logical_not_2: pin names not known; wires that end beside it: rdy, N114
  Multiplexer #(.width(32), .enable("false")) multiplexer_1 (.in0(N81_112), .in1(x), .out(N115_146), .sel(start));
  // Logical_OR_Gate #(.width(1)) logical_or_1: pin names not known; wires that end beside it: start, N114, N113
endmodule
