// Logisim project set.circ as structural Verilog: 7 circuits, main circuit set
module main (
);

  wire clock_1_out, clock_2_out, clock_3_out, set_1_found, set_1_rdy, set_coll_found, set_coll_rdy,
       set_conv_found, set_conv_rdy, tester_1_add, tester_1_clk_out, tester_1_fail, tester_1_find,
       tester_1_reset, tester_1_success, tester_2_add, tester_2_clk_out, tester_2_fail, tester_2_find,
       tester_2_reset, tester_2_success, tester_3_add, tester_3_clk_out, tester_3_fail, tester_3_find,
       tester_3_reset, tester_3_success;
  wire [7:0] tester_1_x, tester_2_x, tester_3_x;

  // Probe on tester_1_find
  // Probe on tester_1_x
  Clock clock_1 (.out(clock_1_out));
  LED led_1 (.in(tester_1_fail));
  set set_1 (
    .reset(tester_1_reset), .clk(tester_1_clk_out), .add(tester_1_add), .find(tester_1_find),
    .rdy(set_1_rdy), .found(set_1_found), .x(tester_1_x));
  tester tester_1 (
    .found(set_1_found), .rdy(set_1_rdy), .clk_in(clock_1_out), .x(tester_1_x), .success(tester_1_success),
    .find(tester_1_find), .fail(tester_1_fail), .clk_out(tester_1_clk_out), .add(tester_1_add),
    .reset(tester_1_reset));
  LED led_2 (.in(tester_1_success));
  // Probe on tester_2_x
  // Probe on tester_2_find
  Clock clock_2 (.out(clock_2_out));
  set_conv set_conv (
    .clk(tester_2_clk_out), .reset(tester_2_reset), .find(tester_2_find), .add(tester_2_add), .x(tester_2_x),
    .rdy(set_conv_rdy), .found(set_conv_found));
  LED led_3 (.in(tester_2_success));
  LED led_4 (.in(tester_2_fail));
  tester tester_2 (
    .found(set_conv_found), .rdy(set_conv_rdy), .clk_in(clock_2_out), .x(tester_2_x),
    .success(tester_2_success), .find(tester_2_find), .fail(tester_2_fail), .clk_out(tester_2_clk_out),
    .add(tester_2_add), .reset(tester_2_reset));
  // Probe on tester_3_x
  // Probe on tester_3_find
  Clock clock_3 (.out(clock_3_out));
  LED led_5 (.in(tester_3_fail));
  set_coll set_coll (
    .clk(tester_3_clk_out), .reset(tester_3_reset), .find(tester_3_find), .add(tester_3_add), .x(tester_3_x),
    .rdy(set_coll_rdy), .found(set_coll_found));
  LED led_6 (.in(tester_3_success));
  tester tester_3 (
    .found(set_coll_found), .rdy(set_coll_rdy), .clk_in(clock_3_out), .x(tester_3_x),
    .success(tester_3_success), .find(tester_3_find), .fail(tester_3_fail), .clk_out(tester_3_clk_out),
    .add(tester_3_add), .reset(tester_3_reset));

  // Notes on the sheet:
  //   Red means failure,
  //   the output bar is
  //   inconsistent with the
  //   timing diagram for
  //   Green means success
  //   Your solution matches
  //   the full timing diagram
  //   Congratulations!
  //   Red means failure,
  //   the output bar is
  //   inconsistent with the
  //   timing diagram for
  //   Green means success
  //   Your solution matches
  //   the full timing diagram
  //   Congratulations!
  //   Red means failure,
  //   the output bar is
  //   inconsistent with the
  //   timing diagram for
  //   Green means success
  //   Your solution matches
  //   the full timing diagram
  //   Congratulations!
endmodule

module set (
  input  [7:0] x,
  input  reset,
  input  clk,
  input  add,
  input  find,
  output rdy,
  output found
);

  wire add_success, adding, and_1_out, and_2_out, and_3_out, and_4_out, comparator_1_eq, comparator_2_eq,
       find_success, finding, not_1_out, or_3_out, or_4_out, or_5_out, or_6_out, or_7_out, or_8_out,
       or_9_out, or_10_out, or_11_out, start, stop, update, valid_slot;
  wire [3:0] adder_1_out, idx_q, multiplexer_1_out, slot;
  wire [7:0] ram_1_data;
  wire [15:0] multiplexer_2_out, multiplexer_3_out, or_1_out, shifter_1_out, valid_q;

  Shifter #(.width(16)) shifter_1 (.in(16'h1), .\dist (slot), .out(shifter_1_out));
  Adder #(.width(4)) adder_1 (.a(slot), .b(4'b0001), .out(adder_1_out));  // open: cin, cout
  assign or_1_out = valid_q | shifter_1_out;  // OR_Gate or_1, 16 bits wide
  Multiplexer #(.width(4), .disabled(0), .enable("false")) multiplexer_1 (
    .in0(adder_1_out), .in1(4'b0000), .out(multiplexer_1_out), .sel(reset));
  or or_2 (start, add, find);
  or or_3 (or_3_out, stop, start);
  or or_4 (or_4_out, start, ~rdy);  // OR_Gate
  Multiplexer #(.width(16), .enable("false")) multiplexer_2 (
    .in0(valid_q), .in1(or_1_out), .out(multiplexer_2_out), .sel(add_success));
  not not_1 (not_1_out, clk);
  Register #(.width(4), .trigger("falling")) idx (
    .D(multiplexer_1_out), .en(update), .Q(idx_q), .clk(clk));  // open: clr
  and and_1 (and_1_out, ~reset, or_4_out, ~stop, find);  // AND_Gate
  and and_2 (and_2_out, ~reset, or_4_out, ~stop, add);  // AND_Gate
  and and_3 (and_3_out, or_3_out, or_4_out);
  Multiplexer #(.width(16), .enable("false")) multiplexer_3 (
    .in0(multiplexer_2_out), .in1({16{1'b0}}), .out(multiplexer_3_out), .sel(reset));
  or or_5 (or_5_out, reset, start, ~rdy);  // OR_Gate
  RAM #(.addrWidth(4), .bus("separate")) ram_1 (
    .addr(slot), .din(x), .data(ram_1_data), .str(add_success), .clk(not_1_out));  // open: sel, ld, clr
  Multiplexer #(.width(4), .disabled(0), .enable("false")) multiplexer_4 (
    .in0(idx_q), .in1(x[3:0]), .out(slot), .sel(or_6_out));
  // Probe on slot
  or or_6 (or_6_out, find, add);
  or or_7 (or_7_out, and_3_out, reset);
  // Probe on valid_q
  Register #(.width(16), .trigger("falling")) valid (
    .D(multiplexer_3_out), .en(or_5_out), .Q(valid_q), .clk(clk));  // open: clr
  Comparator comparator_1 (.a(x), .b(ram_1_data), .eq(comparator_1_eq));  // open: gt, lt
  Comparator #(.width(4)) comparator_2 (.a(slot), .b(x[3:0]), .eq(comparator_2_eq));  // open: gt, lt
  Register #(.width(1), .trigger("falling")) u_finding (
    .D(and_1_out), .en(or_7_out), .Q(finding), .clk(clk));  // open: clr
  Register #(.width(1), .trigger("falling")) u_adding (
    .D(and_2_out), .en(or_7_out), .Q(adding), .clk(clk));  // open: clr
  BitSelector #(.width(16)) bitselector_1 (.in(valid_q), .out(valid_slot), .sel(slot));
  or or_8 (or_8_out, find, finding);
  or or_9 (or_9_out, add, adding);
  and and_4 (and_4_out, comparator_2_eq, ~start);  // AND_Gate
  or or_10 (or_10_out, finding, adding);
  or or_11 (or_11_out, add_success, find_success);
  and and_5 (update, ~reset, or_4_out);  // AND_Gate
  and and_6 (find_success, or_8_out, comparator_1_eq, valid_slot);
  and and_7 (add_success, ~valid_slot, or_9_out);  // AND_Gate
  or or_12 (stop, and_4_out, find_success, add_success, ~valid_slot);  // OR_Gate
  not not_2 (rdy, or_10_out);
  Register #(.width(1), .trigger("falling")) u_found (.D(or_11_out), .en(update), .Q(found), .clk(clk));  // open: clr

  // Other names for the same wires on the sheet: hash[3:0] = x[3:0]

  // Notes on the sheet:
  //   find | add
  //   No modifique esta parte
  //   Es correcta
  //   Valid
  //   handling
  //   Ram
  //   handling
  //   Debe generar estos 3 túneles
  //   Idx
  //   handling
  //   No modifique esta parte
  //   Es correcta
  //   state handling
  //   idx and found
endmodule

module tester (
  input  rdy,
  input  found,
  input  clk_in,
  output [7:0] x,
  output find,
  output add,
  output reset,
  output success,
  output fail,
  output clk_out
);

  wire and_1_out, comparator_1_eq, d_ff_1_qn, or_1_out, or_2_out;
  wire [5:0] counter_1_q;
  wire [31:8] rom_1_data;

  D_Flip_Flop #(.trigger("falling")) d_ff_1 (.clk(clk_in), .D(1'b1), .Qn(d_ff_1_qn));  // open: Q, preset, reset
  or or_1 (or_1_out, d_ff_1_qn, rdy, or_2_out);
  Pull_Resistor pull_resistor_1 (.node(rdy));
  Pull_Resistor pull_resistor_2 (.node(found));
  Counter #(.width(6), .max('h3f), .trigger("falling")) counter_1 (
    .count(and_1_out), .Q(counter_1_q), .clk(clk_in));  // open: load, D, carry, clr
  and and_1 (and_1_out, or_1_out, ~fail, ~success);  // AND_Gate
  ROM #(.addrWidth(6), .dataWidth(32)) rom_1 (
    .addr(counter_1_q),
    .data({rom_1_data[31:29], success, rom_1_data[27:25], reset, rom_1_data[23:17], add, rom_1_data[15:13], find, rom_1_data[11:8], x}));
  // Probe on found
  Comparator #(.width(1), .mode("unsigned")) comparator_1 (
    .a(rom_1_data[20]), .b(found), .eq(comparator_1_eq));  // open: gt, lt
  or or_2 (or_2_out, add, find);
  and and_2 (fail, rom_1_data[8], rdy, ~comparator_1_eq);  // AND_Gate
  LED led_1 (.in(fail));
  LED led_2 (.in(success));
  // Probe on x
  and and_3 (clk_out, ~fail, clk_in);  // AND_Gate

  // Notes on the sheet:
  //   sucess[28:28] reset[24:24] foundRef[20:20] add[16:16] find[12:12] valid[8:8] x[7:0]
  //   contents of rom_1 (hex, n*v repeats v):
  //   0 1005 105 105 10005 100105 100105 100105 1005 100105 100105 10007 100107 100107 1005 100105 1007
  //   100107 100b 10b 1000b 10010b 10003 100103 100b 10010b 1003 100103 1005 100105 1025 125 10025 100125
  //   100125 1035 135 10035 100135 100135 1008 108 108 1006 106 1025 100125 1045 145 1075 175 10ff 1ff
  //   100ff 1001ff 10ff 1001ff 103f 5*13f 1000003f
  //   success
  //   valid
  //   start
  //   foundRef
endmodule

module set_conv (
  input  clk,
  input  reset,
  input  find,
  input  add,
  input  [7:0] x,
  output rdy,
  output found
);

  wire add_success_2_p1, add_success_3_p1, add_success_5_p1, add_success_6_p1, add_success_p1, adding,
       auto_247_y, auto_343_out, auto_349_out, comparator_1_eq, find_success, finding, logical_and_1_p1,
       logical_and_2_p1, logical_and_3_p1, logical_and_3_p3, logical_and_4_p2, logical_and_4_p3,
       logical_or_7_p3, logical_or_8_p3, multiplexer_15_out, multiplexer_17_out, multiplexer_18_out, N72,
       N73, N75, N77, N78_2_p1, N78_3_p1, N78_4_p1, N78_5_p1, N78_6_p1, N78_p1, N99, N108, N117, N126, N135,
       N144, N153, N162, N171, N180, N189, N198, N207, N216, N225, N234, N243, N252_2_p1, N252_3_p1, N252_p1,
       N253, N254_2_p1, N254_3_p1, N254_p1, N256_2_p1, N256_3_p1, N256_p1, N257, N258_2_p1, N258_3_p1,
       N258_p1, N260, N261, N262, N263, N264, N265, N266, N267, N268, N269, N270, N271, N272, N273, N274,
       N275, N276, N277, N278, N279, N280, N281, N282, N283, N285_2_p1, N285_3_p1, N285_4_p1, N285_5_p1,
       N285_6_p1, N285_p1, N297, N303, N306, N307, N421, N483, slot_2_p1, slot_16_2_p1, slot_16_3_p1,
       slot_16_4_p1, slot_16_5_p1, slot_16_6_p1, slot_16_7_p1, slot_16_8_p1, slot_16_p1, slot_17_2_p1,
       slot_17_3_p1, slot_17_4_p1, slot_17_p1, slot_18_2_p1, slot_18_p1, slot_19_p1, stop_2_p1, stop_p1,
       valid_slot, X_UNDEF_1_6312_p1, X_UNDEF_1_6354_p1;
  wire [1:0] N78_286_p1, N78_287_p1, N284_285_p1;
  wire [3:0] adder_1_out, hash_2_p1, hash_p1, idx, multiplexer_19_out, multiplexer_20_out,
       multiplexer_25_out, multiplexer_27_out, slot_4_p1, slot_p1, X_UNDEF_4_2792_p1, X_UNDEF_4_6025_p1,
       X_UNDEF_4_6880_p1;
  wire [7:0] auto_470_q, auto_471_q, multiplexer_1_out, multiplexer_2_out, multiplexer_6_out,
       multiplexer_7_out, multiplexer_8_out, multiplexer_9_out, multiplexer_21_out, N100_107, N317_324,
       N333_340, N341_348, N357_364, N365_372, N389_396, N397_404, N405_412, N413_420, N484_491, ram_0,
       ram_1, ram_2, ram_3, ram_4, ram_5, ram_6, ram_9, ram_10, ram_11, ram_12, ram_13, ram_14, ram_15,
       x_2_p1, x_3_p1, X_UNDEF_8_1560_p1, X_UNDEF_8_3695_p1, X_UNDEF_8_9336_p1;
  wire [15:0] and_66_out, auto_261_q, N454_469, not_65_out, or_67_out;
  wire [31:0] negator_1_out, slot_16_19_28_b0_p1;

  // BitLabeledTunnel #(.width(8), .bitSpecs("N6,N7,N8,N9,N10,N11,N12,N13")) x: pin names not known; wires that end beside it: x
  // BitLabeledTunnel #(.width(8), .bitSpecs("N6,N7,N8,N9,N10,N11,N12,N13"), .\output ("true")) x_2: pin names not known; wires that end beside it: x_2_p1
  Comparator #(.mode("unsigned")) comparator_1 (
    .a(multiplexer_1_out), .b(x_2_p1), .eq(comparator_1_eq));  // open: gt, lt
  // BitLabeledTunnel #(.width(4), .bitSpecs("N16,N17,N18,N19"), .\output ("true")) slot: pin names not known; wires that end beside it: slot_p1
  Adder #(.width(4)) adder_1 (.a(slot_p1), .b(4'b0001), .out(adder_1_out));  // open: cin, cout
  // BitLabeledTunnel #(.bitSpecs("N252"), .\output ("true")) N252: pin names not known; wires that end beside it: N252_p1
  // BitLabeledTunnel #(.bitSpecs("N256"), .\output ("true")) N256: pin names not known; wires that end beside it: N256_p1
  // BitLabeledTunnel #(.bitSpecs("N258"), .\output ("true")) N258: pin names not known; wires that end beside it: N258_p1
  // BitLabeledTunnel #(.bitSpecs("N254"), .\output ("true")) N254: pin names not known; wires that end beside it: N254_p1
  Multiplexer #(.width(8), .enable("false")) multiplexer_1 (
    .in0(multiplexer_2_out), .in1(N317_324), .out(multiplexer_1_out), .sel(slot_19_p1));
  // BitLabeledTunnel #(.bitSpecs("N19"), .\output ("true")) slot_19: pin names not known; wires that end beside it: slot_19_p1
  not auto_341 (N253, N252_p1);
  not auto_347 (N257, N256_p1);
  not auto_349 (auto_349_out, N258_p1);
  not auto_343 (auto_343_out, N254_p1);
  assign and_66_out = auto_261_q & not_65_out;  // AND_Gate and_66, 16 bits wide
  // BitLabeledTunnel #(.bitSpecs("N252"), .\output ("true")) N252_2: pin names not known; wires that end beside it: N252_2_p1
  // BitLabeledTunnel #(.bitSpecs("N256"), .\output ("true")) N256_2: pin names not known; wires that end beside it: N256_2_p1
  // BitLabeledTunnel #(.bitSpecs("N258"), .\output ("true")) N258_2: pin names not known; wires that end beside it: N258_2_p1
  // BitLabeledTunnel #(.bitSpecs("N254"), .\output ("true")) N254_2: pin names not known; wires that end beside it: N254_2_p1
  // BitLabeledTunnel #(.bitSpecs("N258"), .\output ("true")) N258_3: pin names not known; wires that end beside it: N258_3_p1
  // BitLabeledTunnel #(.bitSpecs("N252"), .\output ("true")) N252_3: pin names not known; wires that end beside it: N252_3_p1
  // BitLabeledTunnel #(.bitSpecs("N254"), .\output ("true")) N254_3: pin names not known; wires that end beside it: N254_3_p1
  // BitLabeledTunnel #(.bitSpecs("N256"), .\output ("true")) N256_3: pin names not known; wires that end beside it: N256_3_p1
  // BitLabeledTunnel #(.width(32), .bitSpecs("N16,N17,N18,N19,0,0,0,0,0,0,0,0,0,0,0,0,0,0,0,0,0,0,0,0,0,0,0,0,0,0,0,0"), .\output ("true")) slot_16_19_28_b0: pin names not known; wires that end beside it: slot_16_19_28_b0_p1
  // BitLabeledTunnel #(.bitSpecs("N78"), .\output ("true")) N78: pin names not known; wires that end beside it: N78_p1
  // Logical_AND_Gate #(.width(1)) logical_and_1: pin names not known; wires that end beside it: logical_and_1_p1, comparator_1_eq, find_success
  Multiplexer #(.width(8), .enable("false")) multiplexer_2 (
    .in0(multiplexer_6_out), .in1(N333_340), .out(multiplexer_2_out), .sel(slot_18_p1));
  // BitLabeledTunnel #(.bitSpecs("N18"), .\output ("true")) slot_18: pin names not known; wires that end beside it: slot_18_p1
  and auto_361 (N263, N252_2_p1, auto_343_out);
  and auto_345 (N260, N253, auto_343_out);
  and auto_443 (N279, N256_2_p1, N258_2_p1);
  and auto_371 (N265, N253, N254_2_p1);
  and auto_351 (N261, N257, auto_349_out);
  and auto_417 (N274, N257, N258_3_p1);
  and auto_379 (N267, N252_3_p1, N254_3_p1);
  and auto_389 (N269, N256_3_p1, auto_349_out);
  Multiplexer #(.width(8), .enable("false")) multiplexer_3 (
    .in0(N341_348), .in1(multiplexer_7_out), .out(N317_324), .sel(slot_18_2_p1));
  // BitLabeledTunnel #(.bitSpecs("N18"), .\output ("true")) slot_18_2: pin names not known; wires that end beside it: slot_18_2_p1
  Register #(.trigger("falling"), .resetType("noReset")) auto_469 (
    .D(N100_107), .en(N108), .Q(ram_9), .clk(clk));  // open: clr
  Negator #(.width(32), .signMode("signed")) negator_1 (.in(slot_16_19_28_b0_p1), .out(negator_1_out));
  Register #(.width(1), .trigger("falling"), .resetType("syncReset")) auto_245 (
    .D(N72), .en(N73), .Q(adding), .clk(clk), .clr(reset));
  Register #(.width(1), .trigger("falling"), .resetType("syncReset")) auto_257 (
    .D(N77), .en(N78_p1), .Q(found), .clk(clk), .clr(reset));
  Register #(.width(16), .trigger("falling"), .resetType("syncReset")) auto_261 (
    .D(or_67_out), .en(N99), .Q(auto_261_q), .clk(clk), .clr(reset));
  assign not_65_out = ~N454_469;  // NOT_Gate not_65, 16 bits wide
  // Logical_AND_Gate #(.width(1)) logical_and_2: pin names not known; wires that end beside it: logical_and_2_p1, valid_slot, logical_and_1_p1
  Multiplexer #(.width(8), .enable("false")) multiplexer_4 (
    .in0(multiplexer_9_out), .in1(multiplexer_8_out), .out(N333_340), .sel(slot_17_p1));
  // BitLabeledTunnel #(.bitSpecs("N17"), .\output ("true")) slot_17: pin names not known; wires that end beside it: slot_17_p1
  and auto_451 (N281, N263, N279);
  and auto_445 (N280, N260, N279);
  and auto_363 (N264, N263, N261);
  and auto_457 (N282, N265, N279);
  and auto_425 (N276, N263, N274);
  and auto_353 (N262, N260, N261);
  and auto_373 (N266, N265, N261);
  and auto_419 (N275, N260, N274);
  // Logical_NOT_Gate #(.width(1)) logical_not_1: pin names not known; wires that end beside it: N306, rdy
  Multiplexer #(.width(8), .enable("false")) multiplexer_5 (
    .in0(N389_396), .in1(N397_404), .out(N341_348), .sel(slot_17_2_p1));
  // BitLabeledTunnel #(.bitSpecs("N17"), .\output ("true")) slot_17_2: pin names not known; wires that end beside it: slot_17_2_p1
  and auto_397 (N271, N263, N269);
  and auto_391 (N270, N260, N269);
  and auto_463 (N283, N267, N279);
  and auto_431 (N277, N265, N274);
  and auto_403 (N272, N265, N269);
  and auto_381 (N268, N267, N261);
  and auto_437 (N278, N267, N274);
  and auto_409 (N273, N267, N269);
  Register #(.trigger("falling"), .resetType("noReset")) auto_471 (
    .D(N100_107), .en(N126), .Q(auto_471_q), .clk(clk));  // open: clr
  Multiplexer #(.width(8), .enable("false")) multiplexer_6 (
    .in0(N357_364), .in1(N365_372), .out(multiplexer_6_out), .sel(slot_17_3_p1));
  // BitLabeledTunnel #(.bitSpecs("N17"), .\output ("true")) slot_17_3: pin names not known; wires that end beside it: slot_17_3_p1
  Register #(.trigger("falling"), .resetType("noReset")) auto_472 (
    .D(N100_107), .en(N135), .Q(ram_6), .clk(clk));  // open: clr
  Register #(.trigger("falling"), .resetType("noReset")) auto_479 (
    .D(N100_107), .en(N198), .Q(ram_14), .clk(clk));  // open: clr
  Register #(.trigger("falling"), .resetType("noReset")) auto_480 (
    .D(N100_107), .en(N207), .Q(ram_13), .clk(clk));  // open: clr
  Register #(.trigger("falling"), .resetType("noReset")) auto_476 (
    .D(N100_107), .en(N171), .Q(ram_2), .clk(clk));  // open: clr
  Register #(.trigger("falling"), .resetType("noReset")) auto_474 (
    .D(N100_107), .en(N153), .Q(ram_4), .clk(clk));  // open: clr
  Register #(.trigger("falling"), .resetType("noReset")) auto_470 (
    .D(N100_107), .en(N117), .Q(auto_470_q), .clk(clk));  // open: clr
  Register #(.trigger("falling"), .resetType("noReset")) auto_482 (
    .D(N100_107), .en(N225), .Q(ram_11), .clk(clk));  // open: clr
  Register #(.trigger("falling"), .resetType("noReset")) auto_481 (
    .D(N100_107), .en(N216), .Q(ram_12), .clk(clk));  // open: clr
  Multiplexer #(.width(8), .enable("false")) multiplexer_7 (
    .in0(N405_412), .in1(N413_420), .out(multiplexer_7_out), .sel(slot_17_4_p1));
  // BitLabeledTunnel #(.bitSpecs("N17"), .\output ("true")) slot_17_4: pin names not known; wires that end beside it: slot_17_4_p1
  Register #(.trigger("falling"), .resetType("noReset")) auto_473 (
    .D(N100_107), .en(N144), .Q(ram_5), .clk(clk));  // open: clr
  Register #(.trigger("falling"), .resetType("noReset")) auto_477 (
    .D(N100_107), .en(N180), .Q(ram_1), .clk(clk));  // open: clr
  Register #(.trigger("falling"), .resetType("noReset")) auto_484 (
    .D(N100_107), .en(N243), .Q(ram_0), .clk(clk));  // open: clr
  Register #(.trigger("falling"), .resetType("noReset")) auto_478 (
    .D(N100_107), .en(N189), .Q(ram_15), .clk(clk));  // open: clr
  Register #(.trigger("falling"), .resetType("noReset")) auto_475 (
    .D(N100_107), .en(N162), .Q(ram_3), .clk(clk));  // open: clr
  Register #(.trigger("falling"), .resetType("noReset")) auto_483 (
    .D(N100_107), .en(N234), .Q(ram_10), .clk(clk));  // open: clr
  Register #(.width(1), .trigger("falling"), .resetType("syncReset")) auto_251 (
    .D(N75), .en(N73), .Q(finding), .clk(clk), .clr(reset));
  // BitLabeledTunnel #(.width(2), .bitSpecs("N284,N285"), .\output ("true")) N284_285: pin names not known; wires that end beside it: N284_285_p1
  ys_reduce_bool_W2 auto_247 (.A(N284_285_p1), .Y(auto_247_y));
  // BitLabeledTunnel #(.bitSpecs("N286")) N286: pin names not known; wires that end beside it: auto_247_y
  Register #(.width(4), .trigger("falling"), .resetType("syncReset")) auto_260 (
    .D(adder_1_out), .en(N78_2_p1), .Q(idx), .clk(clk), .clr(reset));
  // BitLabeledTunnel #(.bitSpecs("N78"), .\output ("true")) N78_2: pin names not known; wires that end beside it: N78_2_p1, 1'b1
  // Dynamic_Shifter #(.aWidth(1), .bWidth(32), .yWidth(16), .bSigned("true")) dynamic_shifter_1: pin names not known; wires that end beside it: negator_1_out, N454_469
  ys_reduce_and_W2 auto_263 (.A(N78_287_p1), .Y(N99));
  // BitLabeledTunnel #(.width(2), .bitSpecs("N287,N78"), .\output ("true")) N78_287: pin names not known; wires that end beside it: N78_287_p1
  assign or_67_out = and_66_out | N454_469;  // OR_Gate or_67, 16 bits wide
  // BitLabeledTunnel #(.width(4), .bitSpecs("N16,N17,N18,N19"), .\output ("true")) slot_2: pin names not known; wires that end beside it: slot_2_p1, auto_261_q, slot_2_p1
  Multiplexer #(.width(8), .enable("false")) multiplexer_8 (
    .in0(ram_6), .in1(auto_471_q), .out(multiplexer_8_out), .sel(slot_16_p1));
  // BitLabeledTunnel #(.bitSpecs("N16"), .\output ("true")) slot_16: pin names not known; wires that end beside it: slot_16_p1
  Multiplexer #(.width(8), .enable("false")) multiplexer_9 (
    .in0(ram_4), .in1(ram_5), .out(multiplexer_9_out), .sel(slot_16_2_p1));
  // BitLabeledTunnel #(.bitSpecs("N16"), .\output ("true")) slot_16_2: pin names not known; wires that end beside it: slot_16_2_p1
  Multiplexer #(.width(8), .enable("false")) multiplexer_10 (
    .in0(auto_470_q), .in1(ram_9), .out(N389_396), .sel(slot_16_3_p1));
  // BitLabeledTunnel #(.bitSpecs("N16"), .\output ("true")) slot_16_3: pin names not known; wires that end beside it: slot_16_3_p1
  // Dynamic_Shifter #(.aWidth(16), .bWidth(4), .yWidth(1), .mode("shiftx")) dynamic_shifter_2: pin names not known; wires that end beside it: valid_slot
  Multiplexer #(.width(8), .enable("false")) multiplexer_11 (
    .in0(ram_2), .in1(ram_3), .out(N365_372), .sel(slot_16_4_p1));
  // BitLabeledTunnel #(.bitSpecs("N16"), .\output ("true")) slot_16_4: pin names not known; wires that end beside it: slot_16_4_p1
  Multiplexer #(.width(8), .enable("false")) multiplexer_12 (
    .in0(ram_14), .in1(ram_15), .out(N413_420), .sel(slot_16_5_p1));
  // BitLabeledTunnel #(.bitSpecs("N16"), .\output ("true")) slot_16_5: pin names not known; wires that end beside it: slot_16_5_p1
  // Logical_OR_Gate #(.width(1)) logical_or_1: pin names not known; wires that end beside it: find, finding, logical_and_2_p1
  // Logical_OR_Gate #(.width(1)) logical_or_2: pin names not known; wires that end beside it: N307
  // BitLabeledTunnel #(.bitSpecs("N287"), .\output ("true")) add_success: pin names not known; wires that end beside it: add_success_p1, find_success, add_success_p1
  // Logical_OR_Gate #(.width(1)) logical_or_3: pin names not known; wires that end beside it: finding, adding, N306
  Multiplexer #(.width(8), .enable("false")) multiplexer_13 (
    .in0(ram_10), .in1(ram_11), .out(N397_404), .sel(slot_16_6_p1));
  // BitLabeledTunnel #(.bitSpecs("N16"), .\output ("true")) slot_16_6: pin names not known; wires that end beside it: slot_16_6_p1
  or or_69 (N77, find_success, add_success_2_p1);
  // BitLabeledTunnel #(.bitSpecs("N287"), .\output ("true")) add_success_2: pin names not known; wires that end beside it: add_success_2_p1
  // BitLabeledTunnel #(.bitSpecs("N285"), .\output ("true")) N285: pin names not known; wires that end beside it: N285_p1, N285_p1, N306
  // BitLabeledTunnel #(.bitSpecs("N78")) N78_3: pin names not known; wires that end beside it: N78_3_p1
  // Logical_OR_Gate #(.width(1)) logical_or_4: pin names not known; wires that end beside it: N78_3_p1
  Multiplexer #(.width(8), .enable("false")) multiplexer_14 (
    .in0(ram_12), .in1(ram_13), .out(N405_412), .sel(slot_16_7_p1));
  // BitLabeledTunnel #(.bitSpecs("N16"), .\output ("true")) slot_16_7: pin names not known; wires that end beside it: slot_16_7_p1
  // BitLabeledTunnel #(.bitSpecs("x"), .\output ("true")) X_UNDEF_1_6354: pin names not known; wires that end beside it: X_UNDEF_1_6354_p1
  Multiplexer #(.enable("false")) multiplexer_15 (
    .in0(X_UNDEF_1_6354_p1), .in1(add), .out(multiplexer_15_out), .sel(N285_2_p1));
  // BitLabeledTunnel #(.bitSpecs("N285"), .\output ("true")) N285_2: pin names not known; wires that end beside it: N285_2_p1
  Multiplexer #(.width(8), .enable("false")) multiplexer_16 (
    .in0(ram_0), .in1(ram_1), .out(N357_364), .sel(slot_16_8_p1));
  // BitLabeledTunnel #(.bitSpecs("N16"), .\output ("true")) slot_16_8: pin names not known; wires that end beside it: slot_16_8_p1
  // BitLabeledTunnel #(.bitSpecs("N285")) N285_3: pin names not known; wires that end beside it: N285_3_p1
  // Logical_OR_Gate #(.width(1)) logical_or_5: pin names not known; wires that end beside it: find, add, N285_3_p1
  // BitLabeledTunnel #(.bitSpecs("x"), .\output ("true")) X_UNDEF_1_6312: pin names not known; wires that end beside it: X_UNDEF_1_6312_p1
  Multiplexer #(.enable("false")) multiplexer_17 (
    .in0(X_UNDEF_1_6312_p1), .in1(find), .out(multiplexer_17_out), .sel(N285_4_p1));
  // BitLabeledTunnel #(.bitSpecs("N285"), .\output ("true")) N285_4: pin names not known; wires that end beside it: N285_4_p1
  ys_reduce_and_W2 auto_249 (.A(N78_286_p1), .Y(N73));
  // BitLabeledTunnel #(.width(2), .bitSpecs("N78,N286"), .\output ("true")) N78_286: pin names not known; wires that end beside it: N78_286_p1
  Multiplexer #(.enable("false")) multiplexer_18 (
    .in0(1'b0), .in1(1'b1), .out(multiplexer_18_out), .sel(add_success_3_p1));
  // BitLabeledTunnel #(.bitSpecs("N287"), .\output ("true")) add_success_3: pin names not known; wires that end beside it: add_success_3_p1
  Multiplexer #(.width(4), .enable("false")) multiplexer_19 (
    .in0(idx), .in1(hash_p1), .out(multiplexer_19_out), .sel(N285_5_p1));
  // BitLabeledTunnel #(.width(4), .bitSpecs("N16,N17,N18,N19")) slot_3: pin names not known; wires that end beside it: multiplexer_19_out
  // BitLabeledTunnel #(.width(4), .bitSpecs("N6,N7,N8,N9"), .\output ("true")) hash: pin names not known; wires that end beside it: hash_p1
  // BitLabeledTunnel #(.bitSpecs("N285"), .\output ("true")) N285_5: pin names not known; wires that end beside it: N285_5_p1
  // Logical_AND_Gate #(.width(1)) logical_and_3: pin names not known; wires that end beside it: logical_and_3_p1, N303, logical_and_3_p3
  // BitLabeledTunnel #(.bitSpecs("N287")) add_success_4: pin names not known; wires that end beside it: logical_and_3_p3
  Comparator #(.width(4), .mode("unsigned")) comparator_2 (.a(idx), .b(hash_2_p1), .eq(N297));  // open: gt, lt
  // BitLabeledTunnel #(.width(4), .bitSpecs("N6,N7,N8,N9"), .\output ("true")) hash_2: pin names not known; wires that end beside it: hash_2_p1
  // BitLabeledTunnel #(.width(4), .bitSpecs("x,x,x,x"), .\output ("true")) X_UNDEF_4_6025: pin names not known; wires that end beside it: X_UNDEF_4_6025_p1
  Multiplexer #(.width(4), .enable("false")) multiplexer_20 (
    .in0(X_UNDEF_4_6025_p1), .in1(slot_4_p1), .out(multiplexer_20_out), .sel(add_success_5_p1));
  // BitLabeledTunnel #(.width(4), .bitSpecs("N16,N17,N18,N19"), .\output ("true")) slot_4: pin names not known; wires that end beside it: slot_4_p1
  // BitLabeledTunnel #(.bitSpecs("N287"), .\output ("true")) add_success_5: pin names not known; wires that end beside it: add_success_5_p1
  // BitLabeledTunnel #(.width(8), .bitSpecs("x,x,x,x,x,x,x,x"), .\output ("true")) X_UNDEF_8_1560: pin names not known; wires that end beside it: X_UNDEF_8_1560_p1
  Multiplexer #(.width(8), .enable("false")) multiplexer_21 (
    .in0(X_UNDEF_8_1560_p1), .in1(x_3_p1), .out(multiplexer_21_out), .sel(add_success_6_p1));
  // BitLabeledTunnel #(.width(8), .bitSpecs("N6,N7,N8,N9,N10,N11,N12,N13"), .\output ("true")) x_3: pin names not known; wires that end beside it: x_3_p1
  // BitLabeledTunnel #(.bitSpecs("N287"), .\output ("true")) add_success_6: pin names not known; wires that end beside it: add_success_6_p1
  and memory_ram_355 (N243, N262, N421);
  // BitLabeledTunnel #(.width(4), .bitSpecs("x,x,x,x"), .\output ("true")) X_UNDEF_4_2792: pin names not known; wires that end beside it: X_UNDEF_4_2792_p1
  // BitLabeledTunnel #(.width(8), .bitSpecs("x,x,x,x,x,x,x,x"), .\output ("true")) X_UNDEF_8_9336: pin names not known; wires that end beside it: X_UNDEF_8_9336_p1
  and memory_ram_459 (N198, N282, N421);
  and memory_ram_411 (N126, N273, N421);
  and memory_ram_453 (N207, N281, N421);
  and memory_ram_405 (N135, N272, N421);
  and memory_ram_427 (N108, N276, N421);
  and memory_ram_375 (N171, N266, N421);
  and memory_ram_447 (N216, N280, N421);
  and memory_ram_365 (N180, N264, N421);
  and memory_ram_393 (N153, N270, N421);
  and memory_ram_421 (N117, N275, N421);
  and memory_ram_439 (N225, N278, N421);
  and memory_ram_399 (N144, N271, N421);
  and memory_ram_465 (N189, N283, N421);
  // Logical_NOT_Gate #(.width(1)) logical_not_2: pin names not known; wires that end beside it: valid_slot, N303
  and memory_ram_433 (N234, N277, N421);
  and memory_ram_383 (N162, N268, N421);
  Multiplexer #(.enable("false")) multiplexer_22 (.in0(multiplexer_17_out), .in1(1'b0), .out(N75), .sel(stop_p1));
  // BitLabeledTunnel #(.bitSpecs("N284"), .\output ("true")) stop: pin names not known; wires that end beside it: stop_p1
  Multiplexer #(.enable("false")) multiplexer_23 (.in0(multiplexer_15_out), .in1(1'b0), .out(N72), .sel(stop_2_p1));
  // BitLabeledTunnel #(.bitSpecs("N284"), .\output ("true")) stop_2: pin names not known; wires that end beside it: stop_2_p1
  // Logical_OR_Gate #(.width(1)) logical_or_6: pin names not known; wires that end beside it: add, adding, logical_and_3_p1
  Multiplexer #(.enable("false")) multiplexer_24 (.in0(1'b0), .in1(multiplexer_18_out), .out(N483), .sel(N78_4_p1));
  // BitLabeledTunnel #(.bitSpecs("N78"), .\output ("true")) N78_4: pin names not known; wires that end beside it: N78_4_p1
  Multiplexer #(.width(4), .enable("false")) multiplexer_25 (
    .in0(X_UNDEF_4_2792_p1), .in1(multiplexer_20_out), .out(multiplexer_25_out), .sel(N78_5_p1));
  // BitLabeledTunnel #(.bitSpecs("N78"), .\output ("true")) N78_5: pin names not known; wires that end beside it: N78_5_p1
  Multiplexer #(.width(8), .enable("false")) multiplexer_26 (
    .in0(X_UNDEF_8_9336_p1), .in1(multiplexer_21_out), .out(N484_491), .sel(N78_6_p1));
  // BitLabeledTunnel #(.bitSpecs("N78"), .\output ("true")) N78_6: pin names not known; wires that end beside it: N78_6_p1
  // Logical_AND_Gate #(.width(1)) logical_and_4: pin names not known; wires that end beside it: N297, logical_and_4_p2, logical_and_4_p3
  // BitLabeledTunnel #(.width(4), .bitSpecs("x,x,x,x"), .\output ("true")) X_UNDEF_4_6880: pin names not known; wires that end beside it: X_UNDEF_4_6880_p1
  // BitLabeledTunnel #(.bitSpecs("N285"), .\output ("true")) N285_6: pin names not known; wires that end beside it: N285_6_p1, N285_6_p1
  // BitLabeledTunnel #(.width(8), .bitSpecs("x,x,x,x,x,x,x,x"), .\output ("true")) X_UNDEF_8_3695: pin names not known; wires that end beside it: X_UNDEF_8_3695_p1
  Multiplexer #(.width(4), .enable("false")) multiplexer_27 (
    .in0(multiplexer_25_out), .in1(X_UNDEF_4_6880_p1), .out(multiplexer_27_out), .sel(reset));
  // BitLabeledTunnel #(.width(4), .bitSpecs("N252,N254,N256,N258")) N252_254_256_258: pin names not known; wires that end beside it: multiplexer_27_out
  // Logical_OR_Gate #(.width(1)) logical_or_7: pin names not known; wires that end beside it: N307, logical_and_4_p3, logical_or_7_p3
  Multiplexer #(.enable("false")) multiplexer_28 (.in0(N483), .in1(1'b0), .out(N421), .sel(reset));
  // Logical_NOT_Gate #(.width(1)) logical_not_3: pin names not known; wires that end beside it: logical_and_4_p2
  Multiplexer #(.width(8), .enable("false")) multiplexer_29 (
    .in0(N484_491), .in1(X_UNDEF_8_3695_p1), .out(N100_107), .sel(reset));
  // Logical_OR_Gate #(.width(1)) logical_or_8: pin names not known; wires that end beside it: logical_or_7_p3, N303, logical_or_8_p3
  // BitLabeledTunnel #(.bitSpecs("N284")) stop_3: pin names not known; wires that end beside it: logical_or_8_p3
endmodule

module ys_reduce_bool_W2 (
  input  [1:0] A,
  output Y
);

  wire comparator_1_eq;

  not ne0 (Y, comparator_1_eq);
  Comparator #(.width(2), .mode("unsigned")) comparator_1 (.a(A), .b(2'b00), .eq(comparator_1_eq));  // open: gt, lt
endmodule

module ys_reduce_and_W2 (
  input  [1:0] A,
  output Y
);

  Comparator #(.width(2), .mode("unsigned")) comparator_1 (.a(A), .b(2'b11), .eq(Y));  // open: gt, lt
endmodule

module set_coll (
  input  clk,
  input  reset,
  input  find,
  input  add,
  input  [7:0] x,
  output rdy,
  output found
);

  wire add_success_2_p1, add_success_3_p1, add_success_4_p1, add_success_6_p1, add_success_p1, adding,
       auto_249_y, auto_263_y, comparator_1_eq, comparator_2_eq, find_success, finding, logical_and_1_p1,
       logical_and_2_p1, logical_and_2_p3, logical_and_3_p2, logical_and_4_p3, logical_not_1_p1,
       logical_or_7_p3, logical_or_8_p3, multiplexer_1_out, multiplexer_4_out, multiplexer_7_out,
       multiplexer_10_out, N72, N78_2_p1, N78_3_p1, N78_4_p1, N78_5_p1, N78_6_p1, N78_p1, N101_2_p1,
       N101_3_p1, N101_4_p1, N101_5_p1, N101_6_p1, N101_p1, N102_p1, N116, N119, N120, N123, N199, N212,
       or_69_out, slot_4_p1, stop_2_p1, stop_p1, X_UNDEF_1_4834_p1, X_UNDEF_1_6246_p1;
  wire [1:0] N78_102_p1, N78_103_p1, N100_101_p1;
  wire [3:0] adder_1_out, hash_2_p1, hash_p1, idx, multiplexer_3_out, multiplexer_5_out, multiplexer_9_out,
       N208_211_p1, slot_2_p1, slot_5_p1, slot_p1, X_UNDEF_4_3705_p1, X_UNDEF_4_8806_p1, X_UNDEF_4_9389_p1;
  wire [7:0] multiplexer_14_out, N174_181, N187_194, ram_1_data, x_2_p1, x_3_p1, X_UNDEF_8_2811_p2,
       X_UNDEF_8_5059_p1, X_UNDEF_8_7133_p1;
  wire [15:0] and_66_out, dynamic_shifter_1_p3, N83_98, not_65_out, valid;
  wire [31:0] N125_156, slot_16_19_28_b0_p1;

  // BitLabeledTunnel #(.width(8), .bitSpecs("N6,N7,N8,N9,N10,N11,N12,N13")) x: pin names not known; wires that end beside it: x
  assign and_66_out = valid & not_65_out;  // AND_Gate and_66, 16 bits wide
  // BitLabeledTunnel #(.bitSpecs("N78"), .\output ("true")) N78: pin names not known; wires that end beside it: N78_p1
  // BitLabeledTunnel #(.width(4), .bitSpecs("N16,N17,N18,N19"), .\output ("true")) slot: pin names not known; wires that end beside it: slot_p1
  // BitLabeledTunnel #(.width(8), .bitSpecs("N6,N7,N8,N9,N10,N11,N12,N13"), .\output ("true")) x_2: pin names not known; wires that end beside it: x_2_p1
  Register #(.width(1), .trigger("falling"), .resetType("syncReset")) auto_257 (
    .D(or_69_out), .en(N78_p1), .Q(found), .clk(clk), .clr(reset));
  Adder #(.width(4)) adder_1 (.a(slot_p1), .b(4'b0001), .out(adder_1_out));  // open: cin, cout
  Register #(.width(16), .trigger("falling"), .resetType("syncReset")) auto_261 (
    .D(N83_98), .en(auto_263_y), .Q(valid), .clk(clk), .clr(reset));
  Comparator #(.mode("unsigned")) comparator_1 (.a(ram_1_data), .b(x_2_p1), .eq(comparator_1_eq));  // open: gt, lt
  assign not_65_out = ~dynamic_shifter_1_p3;  // NOT_Gate not_65, 16 bits wide
  // BitLabeledTunnel #(.width(2), .bitSpecs("N100,N101"), .\output ("true")) N100_101: pin names not known; wires that end beside it: N100_101_p1
  // BitLabeledTunnel #(.bitSpecs("N78"), .\output ("true")) N78_2: pin names not known; wires that end beside it: N78_2_p1
  // BitLabeledTunnel #(.width(2), .bitSpecs("N103,N78"), .\output ("true")) N78_103: pin names not known; wires that end beside it: N78_103_p1
  // BitLabeledTunnel #(.width(32), .bitSpecs("N16,N17,N18,N19,0,0,0,0,0,0,0,0,0,0,0,0,0,0,0,0,0,0,0,0,0,0,0,0,0,0,0,0"), .\output ("true")) slot_16_19_28_b0: pin names not known; wires that end beside it: slot_16_19_28_b0_p1
  // Logical_NOT_Gate #(.width(1)) logical_not_1: pin names not known; wires that end beside it: logical_not_1_p1, rdy
  // BitLabeledTunnel #(.bitSpecs("N102")) N102: pin names not known; wires that end beside it: N102_p1
  ys_reduce_bool_W2 auto_247 (.A(N100_101_p1), .Y(N102_p1));
  Register #(.width(1), .trigger("falling"), .resetType("syncReset")) auto_245 (
    .D(N72), .en(auto_249_y), .Q(adding), .clk(clk), .clr(reset));
  Register #(.width(4), .trigger("falling"), .resetType("syncReset")) auto_260 (
    .D(adder_1_out), .en(N78_2_p1), .Q(idx), .clk(clk), .clr(reset));
  ys_reduce_and_W2 auto_263 (.A(N78_103_p1), .Y(auto_263_y));
  Negator #(.width(32), .signMode("signed")) negator_1 (.in(slot_16_19_28_b0_p1), .out(N125_156));
  // Logical_AND_Gate #(.width(1)) logical_and_1: pin names not known; wires that end beside it: logical_and_1_p1, comparator_1_eq, find_success
  assign N83_98 = and_66_out | dynamic_shifter_1_p3;  // OR_Gate or_67, 16 bits wide
  // BitLabeledTunnel #(.bitSpecs("N101"), .\output ("true")) N101: pin names not known; wires that end beside it: N101_p1, N101_p1, logical_not_1_p1
  // BitLabeledTunnel #(.bitSpecs("x"), .\output ("true")) X_UNDEF_1_4834: pin names not known; wires that end beside it: X_UNDEF_1_4834_p1
  // BitLabeledTunnel #(.bitSpecs("x"), .\output ("true")) X_UNDEF_1_6246: pin names not known; wires that end beside it: X_UNDEF_1_6246_p1
  // BitLabeledTunnel #(.width(2), .bitSpecs("N78,N102"), .\output ("true")) N78_102: pin names not known; wires that end beside it: N78_102_p1
  // BitLabeledTunnel #(.width(4), .bitSpecs("N6,N7,N8,N9"), .\output ("true")) hash: pin names not known; wires that end beside it: hash_p1
  // BitLabeledTunnel #(.bitSpecs("N103"), .\output ("true")) add_success: pin names not known; wires that end beside it: add_success_p1
  // BitLabeledTunnel #(.width(4), .bitSpecs("x,x,x,x"), .\output ("true")) X_UNDEF_4_3705: pin names not known; wires that end beside it: X_UNDEF_4_3705_p1
  // BitLabeledTunnel #(.width(4), .bitSpecs("N16,N17,N18,N19"), .\output ("true")) slot_2: pin names not known; wires that end beside it: slot_2_p1
  // BitLabeledTunnel #(.width(4), .bitSpecs("N6,N7,N8,N9"), .\output ("true")) hash_2: pin names not known; wires that end beside it: hash_2_p1
  // BitLabeledTunnel #(.width(8), .bitSpecs("x,x,x,x,x,x,x,x"), .\output ("true")) X_UNDEF_8_7133: pin names not known; wires that end beside it: X_UNDEF_8_7133_p1
  // BitLabeledTunnel #(.width(8), .bitSpecs("N6,N7,N8,N9,N10,N11,N12,N13"), .\output ("true")) x_3: pin names not known; wires that end beside it: x_3_p1
  // BitLabeledTunnel #(.bitSpecs("N103"), .\output ("true")) add_success_2: pin names not known; wires that end beside it: add_success_2_p1, find_success, add_success_2_p1
  // BitLabeledTunnel #(.bitSpecs("N78")) N78_3: pin names not known; wires that end beside it: N78_3_p1
  // Logical_OR_Gate #(.width(1)) logical_or_1: pin names not known; wires that end beside it: N78_3_p1
  Multiplexer #(.enable("false")) multiplexer_1 (
    .in0(X_UNDEF_1_4834_p1), .in1(find), .out(multiplexer_1_out), .sel(N101_2_p1));
  // BitLabeledTunnel #(.bitSpecs("N101"), .\output ("true")) N101_2: pin names not known; wires that end beside it: N101_2_p1
  // BitLabeledTunnel #(.bitSpecs("N101")) N101_3: pin names not known; wires that end beside it: N101_3_p1
  // Logical_OR_Gate #(.width(1)) logical_or_2: pin names not known; wires that end beside it: find, add, N101_3_p1
  Register #(.width(1), .trigger("falling"), .resetType("syncReset")) auto_251 (
    .D(multiplexer_7_out), .en(auto_249_y), .Q(finding), .clk(clk), .clr(reset));
  Multiplexer #(.enable("false")) multiplexer_2 (.in0(X_UNDEF_1_6246_p1), .in1(add), .out(N212), .sel(N101_4_p1));
  // BitLabeledTunnel #(.bitSpecs("N101"), .\output ("true")) N101_4: pin names not known; wires that end beside it: N101_4_p1
  ys_reduce_and_W2 auto_249 (.A(N78_102_p1), .Y(auto_249_y));
  Multiplexer #(.width(4), .enable("false")) multiplexer_3 (
    .in0(idx), .in1(hash_p1), .out(multiplexer_3_out), .sel(N101_5_p1));
  // BitLabeledTunnel #(.width(4), .bitSpecs("N16,N17,N18,N19")) slot_3: pin names not known; wires that end beside it: multiplexer_3_out
  // BitLabeledTunnel #(.bitSpecs("N101"), .\output ("true")) N101_5: pin names not known; wires that end beside it: N101_5_p1
  or or_69 (or_69_out, find_success, add_success_p1);
  Multiplexer #(.enable("false")) multiplexer_4 (
    .in0(1'b0), .in1(1'b1), .out(multiplexer_4_out), .sel(add_success_3_p1));
  // BitLabeledTunnel #(.bitSpecs("N103"), .\output ("true")) add_success_3: pin names not known; wires that end beside it: add_success_3_p1
  Multiplexer #(.width(4), .enable("false")) multiplexer_5 (
    .in0(X_UNDEF_4_3705_p1), .in1(slot_2_p1), .out(multiplexer_5_out), .sel(add_success_4_p1));
  // BitLabeledTunnel #(.bitSpecs("N103"), .\output ("true")) add_success_4: pin names not known; wires that end beside it: add_success_4_p1
  // Logical_AND_Gate #(.width(1)) logical_and_2: pin names not known; wires that end beside it: logical_and_2_p1, N119, logical_and_2_p3
  // BitLabeledTunnel #(.bitSpecs("N103")) add_success_5: pin names not known; wires that end beside it: logical_and_2_p3
  Comparator #(.width(4), .mode("unsigned")) comparator_2 (
    .a(idx), .b(hash_2_p1), .eq(comparator_2_eq));  // open: gt, lt
  Multiplexer #(.width(8), .enable("false")) multiplexer_6 (
    .in0(X_UNDEF_8_7133_p1), .in1(x_3_p1), .out(N174_181), .sel(add_success_6_p1));
  // BitLabeledTunnel #(.bitSpecs("N103"), .\output ("true")) add_success_6: pin names not known; wires that end beside it: add_success_6_p1
  // Logical_OR_Gate #(.width(1)) logical_or_3: pin names not known; wires that end beside it: N123
  // Dynamic_Shifter #(.aWidth(1), .bWidth(32), .yWidth(16), .bSigned("true")) dynamic_shifter_1: pin names not known; wires that end beside it: 1'b1, N125_156, dynamic_shifter_1_p3
  // Logical_AND_Gate #(.width(1)) logical_and_3: pin names not known; wires that end beside it: N116, logical_and_3_p2, logical_and_1_p1
  Multiplexer #(.enable("false")) multiplexer_7 (
    .in0(multiplexer_1_out), .in1(1'b0), .out(multiplexer_7_out), .sel(stop_p1));
  // BitLabeledTunnel #(.bitSpecs("N100"), .\output ("true")) stop: pin names not known; wires that end beside it: stop_p1
  // Logical_OR_Gate #(.width(1)) logical_or_4: pin names not known; wires that end beside it: finding, adding, logical_not_1_p1
  Multiplexer #(.enable("false")) multiplexer_8 (.in0(N212), .in1(1'b0), .out(N72), .sel(stop_2_p1));
  // BitLabeledTunnel #(.bitSpecs("N100"), .\output ("true")) stop_2: pin names not known; wires that end beside it: stop_2_p1
  // BitLabeledTunnel #(.width(4), .bitSpecs("x,x,x,x"), .\output ("true")) X_UNDEF_4_8806: pin names not known; wires that end beside it: X_UNDEF_4_8806_p1
  Multiplexer #(.width(4), .enable("false")) multiplexer_9 (
    .in0(X_UNDEF_4_8806_p1), .in1(multiplexer_5_out), .out(multiplexer_9_out), .sel(N78_4_p1));
  // BitLabeledTunnel #(.bitSpecs("N78"), .\output ("true")) N78_4: pin names not known; wires that end beside it: N78_4_p1
  // Logical_OR_Gate #(.width(1)) logical_or_5: pin names not known; wires that end beside it: find, finding, N116
  Multiplexer #(.enable("false")) multiplexer_10 (
    .in0(1'b0), .in1(multiplexer_4_out), .out(multiplexer_10_out), .sel(N78_5_p1));
  // BitLabeledTunnel #(.bitSpecs("N78"), .\output ("true")) N78_5: pin names not known; wires that end beside it: N78_5_p1
  // Logical_OR_Gate #(.width(1)) logical_or_6: pin names not known; wires that end beside it: add, logical_and_2_p1
  // BitLabeledTunnel #(.width(8), .bitSpecs("x,x,x,x,x,x,x,x"), .\output ("true")) X_UNDEF_8_2811: pin names not known; wires that end beside it: adding, X_UNDEF_8_2811_p2
  Multiplexer #(.width(8), .enable("false")) multiplexer_11 (
    .in0(X_UNDEF_8_2811_p2), .in1(N174_181), .out(N187_194), .sel(N78_6_p1));
  // BitLabeledTunnel #(.bitSpecs("N78"), .\output ("true")) N78_6: pin names not known; wires that end beside it: N78_6_p1
  // Logical_AND_Gate #(.width(1)) logical_and_4: pin names not known; wires that end beside it: comparator_2_eq, N120, logical_and_4_p3
  // Logical_NOT_Gate #(.width(1)) logical_not_2: pin names not known; wires that end beside it: logical_and_3_p2, N119
  // Dynamic_Shifter #(.aWidth(16), .bWidth(4), .yWidth(1), .mode("shiftx")) dynamic_shifter_2: pin names not known; wires that end beside it: valid, logical_and_3_p2
  // BitLabeledTunnel #(.width(4), .bitSpecs("N16,N17,N18,N19"), .\output ("true")) slot_4: pin names not known; wires that end beside it: slot_4_p1, slot_4_p1
  // BitLabeledTunnel #(.width(4), .bitSpecs("N208,N209,N210,N211")) N208_211: pin names not known; wires that end beside it: N208_211_p1
  Multiplexer #(.width(4), .enable("false")) multiplexer_12 (
    .in0(multiplexer_9_out), .in1(X_UNDEF_4_9389_p1), .out(N208_211_p1), .sel(reset));
  // BitLabeledTunnel #(.width(4), .bitSpecs("x,x,x,x"), .\output ("true")) X_UNDEF_4_9389: pin names not known; wires that end beside it: X_UNDEF_4_9389_p1
  Multiplexer #(.enable("false")) multiplexer_13 (.in0(multiplexer_10_out), .in1(1'b0), .out(N199), .sel(reset));
  Multiplexer #(.width(8), .enable("false")) multiplexer_14 (
    .in0(N187_194), .in1(X_UNDEF_8_5059_p1), .out(multiplexer_14_out), .sel(reset));
  // BitLabeledTunnel #(.width(8), .bitSpecs("x,x,x,x,x,x,x,x"), .\output ("true")) X_UNDEF_8_5059: pin names not known; wires that end beside it: X_UNDEF_8_5059_p1
  // Logical_NOT_Gate #(.width(1)) logical_not_3: pin names not known; wires that end beside it: N120
  // BitLabeledTunnel #(.bitSpecs("N101"), .\output ("true")) N101_6: pin names not known; wires that end beside it: N101_6_p1, N101_6_p1
  // Logical_OR_Gate #(.width(1)) logical_or_7: pin names not known; wires that end beside it: N123, logical_and_4_p3, logical_or_7_p3
  // BitLabeledTunnel #(.width(4), .bitSpecs("N16,N17,N18,N19"), .\output ("true")) slot_5: pin names not known; wires that end beside it: slot_5_p1
  RAM #(.addrWidth(4), .bus("separate"), .trigger("falling")) ram_1 (
    .addr(slot_5_p1), .din(multiplexer_14_out), .data(ram_1_data), .str(N199), .clk(clk), .ld(1'b1));  // open: sel, clr
  // Logical_OR_Gate #(.width(1)) logical_or_8: pin names not known; wires that end beside it: logical_or_7_p3, N119, logical_or_8_p3
  // BitLabeledTunnel #(.bitSpecs("N100")) stop_3: pin names not known; wires that end beside it: logical_or_8_p3
endmodule
