// Logisim project sr_cell.circ as structural Verilog
module gen_sr (
  input  S,
  input  R,
  output Q
);

  wire auto_13_out, auto_25_out, N6, N8, N9;

  not auto_13 (auto_13_out, S);
  not auto_15 (N6, R);
  and auto_25 (auto_25_out, auto_13_out, N6);
  and auto_31 (N8, auto_13_out, auto_25_out);
  Register #(.width(1), .trigger("low"), .resetType("noReset"), .enablePolarity("enActiveLow")) auto_37 (
    .D(N9), .Q(Q), .clk(N8));  // open: en, clr
  Multiplexer #(.enable("false")) multiplexer_1 (.in0(1'b0), .in1(1'b1), .out(N9), .sel(S));
endmodule
