// Logisim project sum.circ as structural Verilog
module sum (
  input  [31:0] x,
  input  [31:0] y,
  output carry,
  output [31:0] z
);

  wire [8:0] adder_1_out, adder_2_out, adder_3_out, adder_4_out, adder_5_out, adder_7_out, N66_91_98_p1,
       N108_p1, N109_p1, N119_p1, x_2_9_1_b0_p1, x_10_17_1_b0_p1, x_18_25_1_b0_p1, x_26_33_1_b0_p1,
       y_34_41_1_b0_p1, y_42_49_1_b0_p1, y_50_57_1_b0_p1, y_58_65_1_b0_p1;

  // Probe on x
  // BitLabeledTunnel #(.width(32), .bitSpecs("N2,N3,N4,N5,N6,N7,N8,N9,N10,N11,N12,N13,N14,N15,N16,N17,N18,N19,N20,N21,N22,N23,N24,N25,N26,N27,N28,N29,N30,N31,N32,N33")) x: pin names not known; wires that end beside it: x
  // BitLabeledTunnel #(.width(32), .bitSpecs("N34,N35,N36,N37,N38,N39,N40,N41,N42,N43,N44,N45,N46,N47,N48,N49,N50,N51,N52,N53,N54,N55,N56,N57,N58,N59,N60,N61,N62,N63,N64,N65")) y: pin names not known; wires that end beside it: y
  // Probe on y
  // BitLabeledTunnel #(.width(9), .bitSpecs("N34,N35,N36,N37,N38,N39,N40,N41,0"), .\output ("true")) y_34_41_1_b0: pin names not known; wires that end beside it: y_34_41_1_b0_p1
  // BitLabeledTunnel #(.width(9), .bitSpecs("N42,N43,N44,N45,N46,N47,N48,N49,0"), .\output ("true")) y_42_49_1_b0: pin names not known; wires that end beside it: y_42_49_1_b0_p1
  // BitLabeledTunnel #(.width(9), .bitSpecs("N108,0,0,0,0,0,0,0,0"), .\output ("true")) N108: pin names not known; wires that end beside it: N108_p1
  // BitLabeledTunnel #(.width(9), .bitSpecs("N58,N59,N60,N61,N62,N63,N64,N65,0"), .\output ("true")) y_58_65_1_b0: pin names not known; wires that end beside it: y_58_65_1_b0_p1
  // BitLabeledTunnel #(.width(9), .bitSpecs("N2,N3,N4,N5,N6,N7,N8,N9,0"), .\output ("true")) x_2_9_1_b0: pin names not known; wires that end beside it: x_2_9_1_b0_p1
  Adder #(.width(9)) adder_1 (.a(x_2_9_1_b0_p1), .b(y_34_41_1_b0_p1), .out(adder_1_out));  // open: cin, cout
  // BitLabeledTunnel #(.width(9), .bitSpecs("N67,N68,N69,N70,N71,N72,N73,N74,N119")) N67_74_119: pin names not known; wires that end beside it: adder_1_out
  // BitLabeledTunnel #(.width(9), .bitSpecs("N10,N11,N12,N13,N14,N15,N16,N17,0"), .\output ("true")) x_10_17_1_b0: pin names not known; wires that end beside it: x_10_17_1_b0_p1
  Adder #(.width(9)) adder_2 (.a(x_10_17_1_b0_p1), .b(y_42_49_1_b0_p1), .out(adder_2_out));  // open: cin, cout
  Adder #(.width(9)) adder_3 (.a(adder_7_out), .b(N108_p1), .out(adder_3_out));  // open: cin, cout
  // BitLabeledTunnel #(.width(9), .bitSpecs("N83,N84,N85,N86,N87,N88,N89,N90,N109")) N83_90_109: pin names not known; wires that end beside it: adder_3_out
  // BitLabeledTunnel #(.width(9), .bitSpecs("N26,N27,N28,N29,N30,N31,N32,N33,0"), .\output ("true")) x_26_33_1_b0: pin names not known; wires that end beside it: x_26_33_1_b0_p1
  Adder #(.width(9)) adder_4 (.a(x_26_33_1_b0_p1), .b(y_58_65_1_b0_p1), .out(adder_4_out));  // open: cin, cout
  // BitLabeledTunnel #(.width(9), .bitSpecs("N119,0,0,0,0,0,0,0,0"), .\output ("true")) N119: pin names not known; wires that end beside it: N119_p1
  // BitLabeledTunnel #(.width(9), .bitSpecs("N109,0,0,0,0,0,0,0,0"), .\output ("true")) N109: pin names not known; wires that end beside it: N109_p1
  // BitLabeledTunnel #(.width(9), .bitSpecs("N18,N19,N20,N21,N22,N23,N24,N25,0"), .\output ("true")) x_18_25_1_b0: pin names not known; wires that end beside it: x_18_25_1_b0_p1
  // BitLabeledTunnel #(.width(9), .bitSpecs("N50,N51,N52,N53,N54,N55,N56,N57,0"), .\output ("true")) y_50_57_1_b0: pin names not known; wires that end beside it: y_50_57_1_b0_p1
  Adder #(.width(9)) adder_5 (.a(adder_2_out), .b(N119_p1), .out(adder_5_out));  // open: cin, cout
  // BitLabeledTunnel #(.width(9), .bitSpecs("N75,N76,N77,N78,N79,N80,N81,N82,N108")) N75_82_108: pin names not known; wires that end beside it: adder_5_out
  // BitLabeledTunnel #(.width(9), .bitSpecs("N91,N92,N93,N94,N95,N96,N97,N98,N66")) N66_91_98: pin names not known; wires that end beside it: N66_91_98_p1
  Adder #(.width(9)) adder_6 (.a(adder_4_out), .b(N109_p1), .out(N66_91_98_p1));  // open: cin, cout
  Adder #(.width(9)) adder_7 (.a(x_18_25_1_b0_p1), .b(y_50_57_1_b0_p1), .out(adder_7_out));  // open: cin, cout
  // BitLabeledTunnel #(.bitSpecs("N66"), .\output ("true")) carry: pin names not known; wires that end beside it: carry
  // BitLabeledTunnel #(.width(32), .bitSpecs("N67,N68,N69,N70,N71,N72,N73,N74,N75,N76,N77,N78,N79,N80,N81,N82,N83,N84,N85,N86,N87,N88,N89,N90,N91,N92,N93,N94,N95,N96,N97,N98"), .\output ("true")) z: pin names not known; wires that end beside it: z
  // Probe on z
endmodule
